// Logisim project counter.circ as structural Verilog: 3 circuits, main circuit main
module main (
);

  wire button_1_out, reverse_cont_bit_1_out_2, reverse_cont_bit_1_out_3, reverse_cont_bit_2_out_2,
       reverse_cont_bit_2_out_3, reverse_cont_bit_3_out_2, reverse_cont_bit_3_out_3,
       reverse_cont_bit_4_out_2, reverse_cont_bit_4_out_3;

  LED led_1 (.in(reverse_cont_bit_1_out_2));
  LED led_2 (.in(reverse_cont_bit_3_out_2));
  reverse_cont_bit reverse_cont_bit_1 (
    .in_1(reverse_cont_bit_3_out_3), .out_2(reverse_cont_bit_1_out_2), .out_3(reverse_cont_bit_1_out_3));
  LED led_3 (.in(reverse_cont_bit_4_out_2));
  LED led_4 (.in(reverse_cont_bit_2_out_2));
  reverse_cont_bit reverse_cont_bit_2 (
    .in_1(reverse_cont_bit_4_out_3), .out_2(reverse_cont_bit_2_out_2), .out_3(reverse_cont_bit_2_out_3));
  reverse_cont_bit reverse_cont_bit_3 (
    .in_1(reverse_cont_bit_2_out_3), .out_2(reverse_cont_bit_3_out_2), .out_3(reverse_cont_bit_3_out_3));
  Button button_1 (.out(button_1_out));
  reverse_cont_bit reverse_cont_bit_4 (
    .in_1(button_1_out), .out_2(reverse_cont_bit_4_out_2), .out_3(reverse_cont_bit_4_out_3));
endmodule

module count_bit (
  input  in_1,
  output out_2,
  output out_3
);

  wire and_1_out, and_2_out, or_1_out;

  and and_1 (and_1_out, ~out_2, in_1);  // AND_Gate
  or or_1 (or_1_out, and_1_out, and_2_out);
  and and_2 (and_2_out, in_1, out_2);
  S_R_Flip_Flop s_r_ff_1 (
    .S(and_1_out), .clk(or_1_out), .R(and_2_out), .Q(out_2), .Qn(out_3));  // open: preset, reset, en
endmodule

module reverse_cont_bit (
  input  in_1,
  output out_2,
  output out_3
);

  count_bit count_bit_1 (.in_1(in_1), .out_2(out_2), .out_3(out_3));
endmodule
