// Logisim project ligisch....circ as structural Verilog: 14 circuits, main circuit main
module main (
  input  A,
  input  B,
  input  MC_Switch,
  input  DC_Switch,
  input  IO
);

  wire demultiplexer_1_out0, demultiplexer_1_out1, multiplexer_1_out;

  Multiplexer multiplexer_1 (.in0(A), .in1(B), .out(multiplexer_1_out), .sel(MC_Switch), .en(IO));
  Demultiplexer demultiplexer_1 (
    .out0(demultiplexer_1_out0), .out1(demultiplexer_1_out1), .in(multiplexer_1_out), .sel(DC_Switch), .en(IO));
endmodule

module ALU (
);

  wire undriven, undriven_2, undriven_3, undriven_4, undriven_5, undriven_6, undriven_7, undriven_8,
       undriven_9, undriven_10, undriven_11, undriven_12, undriven_13, undriven_14, undriven_15, undriven_16;

  ADD add_1 (
    .in_1(undriven_16), .in_2(undriven_15), .in_3(undriven_14), .in_4(undriven_13), .in_5(undriven_12),
    .in_6(undriven_11), .in_7(undriven_10), .in_8(undriven_9), .in_9(undriven_8), .in_10(undriven_7),
    .in_11(undriven_6), .in_12(undriven_5), .in_13(undriven_4), .in_14(undriven_3), .in_15(undriven_2),
    .in_16(undriven));
  COMP comp_1 (
    .in_1(undriven_16), .in_2(undriven_15), .in_3(undriven_14), .in_4(undriven_13), .in_5(undriven_12),
    .in_6(undriven_11), .in_7(undriven_10), .in_8(undriven_9), .in_9(undriven_8), .in_10(undriven_7),
    .in_11(undriven_6), .in_12(undriven_5), .in_13(undriven_4), .in_14(undriven_3), .in_15(undriven_2),
    .in_16(undriven));  // open: out_17, out_18
endmodule

module ADD (
  input  in_1,
  input  in_2,
  input  in_3,
  input  in_4,
  input  in_5,
  input  in_6,
  input  in_7,
  input  in_8,
  input  in_9,
  input  in_10,
  input  in_11,
  input  in_12,
  input  in_13,
  input  in_14,
  input  in_15,
  input  in_16
);
endmodule

module COMP (
  input  in_1,
  input  in_2,
  input  in_3,
  input  in_4,
  input  in_5,
  input  in_6,
  input  in_7,
  input  in_8,
  input  in_9,
  input  in_10,
  input  in_11,
  input  in_12,
  input  in_13,
  input  in_14,
  input  in_15,
  input  in_16,
  output out_17,
  output out_18
);

  wire bitcomp_1_out_3, bitcomp_1_out_4, bitcomp_2_out_3, bitcomp_2_out_4, bitcomp_3_out_3, bitcomp_3_out_4,
       bitcomp_4_out_3, bitcomp_4_out_4, bitcomp_5_out_3, bitcomp_5_out_4, bitcomp_6_out_3, bitcomp_6_out_4,
       bitcomp_7_out_3, bitcomp_7_out_4, bitcomp_8_out_3, bitcomp_8_out_4;

  BITCOMP bitcomp_1 (.in_1(in_1), .in_2(in_2), .out_3(bitcomp_1_out_3), .out_4(bitcomp_1_out_4));
  BITCOMP bitcomp_2 (.in_1(in_3), .in_2(in_4), .out_3(bitcomp_2_out_3), .out_4(bitcomp_2_out_4));
  BITCOMP bitcomp_3 (.in_1(in_5), .in_2(in_6), .out_3(bitcomp_3_out_3), .out_4(bitcomp_3_out_4));
  BITCOMP bitcomp_4 (.in_1(in_7), .in_2(in_8), .out_3(bitcomp_4_out_3), .out_4(bitcomp_4_out_4));
  BITCOMP bitcomp_5 (.in_1(in_9), .in_2(in_10), .out_3(bitcomp_5_out_3), .out_4(bitcomp_5_out_4));
  BITCOMP bitcomp_6 (.in_1(in_11), .in_2(in_12), .out_3(bitcomp_6_out_3), .out_4(bitcomp_6_out_4));
  BITCOMP bitcomp_7 (.in_1(in_13), .in_2(in_14), .out_3(bitcomp_7_out_3), .out_4(bitcomp_7_out_4));
  BITCOMP bitcomp_8 (.in_1(in_15), .in_2(in_16), .out_3(bitcomp_8_out_3), .out_4(bitcomp_8_out_4));
  _8bitoverride u_8bitoverride_1 (
    .in_1(bitcomp_1_out_4), .in_2(bitcomp_2_out_3), .in_3(bitcomp_2_out_4), .in_4(bitcomp_3_out_3),
    .in_5(bitcomp_3_out_4), .in_6(bitcomp_4_out_3), .in_7(bitcomp_4_out_4), .in_8(bitcomp_5_out_3),
    .in_9(bitcomp_5_out_4), .in_10(bitcomp_6_out_3), .in_12(bitcomp_6_out_4), .in_13(bitcomp_7_out_3),
    .in_14(bitcomp_7_out_4), .in_15(bitcomp_8_out_3), .in_16(bitcomp_8_out_4), .in_11(bitcomp_1_out_3),
    .out_17(out_17), .out_18(out_18));
endmodule

module BITCOMP (
  input  in_1,
  input  in_2,
  output out_3,
  output out_4
);

  wire xor_1_out;

  xor xor_1 (xor_1_out, in_1, in_2);
  and and_1 (out_3, in_1, xor_1_out);
  and and_2 (out_4, xor_1_out, in_2);
endmodule

module RAM (
  input  in_1,
  input  in_2,
  input  in_3,
  input  in_4,
  input  in_5,
  input  in_6,
  input  in_7,
  input  in_8,
  input  in_9,
  input  in_10,
  input  in_11,
  input  in_12,
  input  in_13,
  input  in_14,
  input  in_15,
  input  in_16,
  input  in_17,
  output out_18,
  output out_19,
  output out_20,
  output out_21,
  output out_22,
  output out_23,
  output out_24,
  output out_25
);

  wire and_1_out, and_2_out, and_3_out, and_4_out, and_5_out, and_6_out, and_7_out, and_8_out, and_9_out,
       and_10_out, and_11_out, and_12_out, and_13_out, and_14_out, and_15_out, and_16_out, and_17_out,
       and_18_out, and_19_out, and_20_out, and_21_out, and_22_out, and_23_out, and_24_out,
       n8_bit_matrix_2_out_19, n8_bit_matrix_2_out_20, n8_bit_matrix_2_out_21, n8_bit_matrix_2_out_22,
       n8_bit_matrix_2_out_23, n8_bit_matrix_2_out_24, n8_bit_matrix_2_out_25, n8_bit_matrix_2_out_26;

  and and_1 (and_1_out, ~in_11, ~in_12, ~in_13, ~in_14, ~in_15, ~in_16, ~in_17);  // AND_Gate
  _8_Bit__Matrix u_8_bit_matrix_1 (
    .in_9(in_9), .in_10(in_10), .in_11(and_1_out), .in_12(and_2_out), .in_13(and_3_out), .in_14(and_4_out),
    .in_1(in_8), .in_2(in_7), .in_3(in_6), .in_4(in_5), .in_5(in_4), .in_6(in_3), .in_7(in_2), .in_8(in_1),
    .out_19(out_25), .out_20(out_24), .out_21(out_23), .out_22(out_22), .out_23(out_21), .out_24(out_20),
    .out_25(out_19), .out_26(out_18), .in_15(and_5_out), .in_16(and_7_out), .in_17(and_6_out),
    .in_18(and_8_out));
  and and_2 (and_2_out, ~in_11, ~in_12, ~in_13, ~in_14, ~in_15, ~in_16, in_17);  // AND_Gate
  and and_3 (and_3_out, ~in_11, ~in_12, ~in_13, ~in_14, ~in_15, in_16, ~in_17);  // AND_Gate
  and and_4 (and_4_out, ~in_11, ~in_12, ~in_13, ~in_14, ~in_15, in_16, in_17);  // AND_Gate
  and and_5 (and_5_out, ~in_11, ~in_12, ~in_13, ~in_14, in_15, ~in_16, ~in_17);  // AND_Gate
  and and_6 (and_6_out, ~in_11, ~in_12, ~in_13, ~in_14, in_15, in_16, in_17);  // AND_Gate
  and and_7 (and_7_out, ~in_11, ~in_12, ~in_13, ~in_14, in_15, ~in_16, in_17);  // AND_Gate
  and and_8 (and_8_out, ~in_11, ~in_12, ~in_13, in_14, ~in_15, ~in_16, ~in_17);  // AND_Gate
  and and_9 (and_9_out, ~in_11, ~in_12, ~in_13, in_14, ~in_15, ~in_16, in_17);  // AND_Gate
  _8_Bit__Matrix u_8_bit_matrix_2 (
    .in_9(in_9), .in_10(in_10), .in_11(and_9_out), .in_12(and_10_out), .in_13(and_11_out),
    .in_14(and_12_out), .in_1(in_8), .in_2(in_7), .in_3(in_6), .in_4(in_5), .in_5(in_4), .in_6(in_3),
    .in_7(in_2), .in_8(in_1), .out_19(n8_bit_matrix_2_out_19), .out_20(n8_bit_matrix_2_out_20),
    .out_21(n8_bit_matrix_2_out_21), .out_22(n8_bit_matrix_2_out_22), .out_23(n8_bit_matrix_2_out_23),
    .out_24(n8_bit_matrix_2_out_24), .out_25(n8_bit_matrix_2_out_25), .out_26(n8_bit_matrix_2_out_26),
    .in_15(and_13_out), .in_16(and_15_out), .in_17(and_14_out), .in_18(and_16_out));
  and and_10 (and_10_out, ~in_11, ~in_12, ~in_13, in_14, ~in_15, in_16, ~in_17);  // AND_Gate
  and and_11 (and_11_out, ~in_11, ~in_12, ~in_13, in_14, ~in_15, in_16, in_17);  // AND_Gate
  and and_12 (and_12_out, ~in_11, ~in_12, ~in_13, in_14, in_15, ~in_16, ~in_17);  // AND_Gate
  and and_13 (and_13_out, ~in_11, ~in_12, ~in_13, in_14, in_15, ~in_16, in_17);  // AND_Gate
  and and_14 (and_14_out, ~in_11, ~in_12, ~in_13, in_14, in_15, in_16, in_17);  // AND_Gate
  and and_15 (and_15_out, ~in_11, ~in_12, ~in_13, in_14, in_15, in_16, ~in_17);  // AND_Gate
  and and_16 (and_16_out, ~in_11, ~in_12, in_13, ~in_14, ~in_15, ~in_16, ~in_17);  // AND_Gate
  and and_17 (and_17_out, ~in_11, ~in_12, in_13, ~in_14, ~in_15, ~in_16, in_17);  // AND_Gate
  _8_Bit__Matrix u_8_bit_matrix_3 (
    .in_9(in_9), .in_10(in_10), .in_11(and_17_out), .in_12(and_18_out), .in_13(and_19_out),
    .in_14(and_20_out), .in_1(in_8), .in_2(in_7), .in_3(in_6), .in_4(in_5), .in_5(in_4), .in_6(in_3),
    .in_7(in_2), .in_8(in_1), .out_19(n8_bit_matrix_2_out_19), .out_20(n8_bit_matrix_2_out_20),
    .out_21(n8_bit_matrix_2_out_21), .out_22(n8_bit_matrix_2_out_22), .out_23(n8_bit_matrix_2_out_23),
    .out_24(n8_bit_matrix_2_out_24), .out_25(n8_bit_matrix_2_out_25), .out_26(n8_bit_matrix_2_out_26),
    .in_15(and_21_out), .in_16(and_23_out), .in_17(and_22_out), .in_18(and_24_out));
  and and_18 (and_18_out, ~in_11, ~in_12, in_13, ~in_14, ~in_15, in_16, ~in_17);  // AND_Gate
  and and_19 (and_19_out, ~in_11, ~in_12, in_13, ~in_14, ~in_15, in_16, in_17);  // AND_Gate
  and and_20 (and_20_out, ~in_11, ~in_12, in_13, ~in_14, in_15, ~in_16, ~in_17);  // AND_Gate
  and and_21 (and_21_out, ~in_11, ~in_12, in_13, ~in_14, in_15, ~in_16, in_17);  // AND_Gate
  and and_22 (and_22_out, ~in_11, ~in_12, in_13, ~in_14, in_15, in_16, in_17);  // AND_Gate
  and and_23 (and_23_out, ~in_11, ~in_12, in_13, ~in_14, in_15, in_16, ~in_17);  // AND_Gate
  and and_24 (and_24_out, ~in_11, ~in_12, in_13, in_14, ~in_15, ~in_16, ~in_17);  // AND_Gate
endmodule

module _8_Bit__Matrix (
  input  in_1,
  input  in_2,
  input  in_3,
  input  in_4,
  input  in_5,
  input  in_6,
  input  in_7,
  input  in_8,
  input  in_9,
  input  in_10,
  input  in_11,
  input  in_12,
  input  in_13,
  input  in_14,
  input  in_15,
  input  in_16,
  input  in_17,
  input  in_18,
  output out_19,
  output out_20,
  output out_21,
  output out_22,
  output out_23,
  output out_24,
  output out_25,
  output out_26
);

  wire and_1_out, and_2_out, and_3_out, and_4_out, and_5_out, and_6_out, and_7_out, and_8_out, and_9_out,
       and_10_out, and_11_out, and_12_out, and_13_out, and_14_out, and_15_out, and_16_out, button_1_out,
       n8_bit_register_1_out_27, n8_bit_register_1_out_28, n8_bit_register_1_out_29,
       n8_bit_register_1_out_30, n8_bit_register_1_out_31, n8_bit_register_1_out_32,
       n8_bit_register_1_out_33, n8_bit_register_1_out_34, n8_bit_register_2_out_19,
       n8_bit_register_2_out_20, n8_bit_register_2_out_21, n8_bit_register_2_out_22,
       n8_bit_register_2_out_23, n8_bit_register_2_out_24, n8_bit_register_2_out_25,
       n8_bit_register_2_out_26, n8_bit_register_2_out_27, n8_bit_register_2_out_28,
       n8_bit_register_2_out_29, n8_bit_register_2_out_30, n8_bit_register_2_out_31,
       n8_bit_register_2_out_32, n8_bit_register_2_out_33, n8_bit_register_2_out_34,
       n8_bit_register_3_out_19, n8_bit_register_3_out_20, n8_bit_register_3_out_21,
       n8_bit_register_3_out_22, n8_bit_register_3_out_23, n8_bit_register_3_out_24,
       n8_bit_register_3_out_25, n8_bit_register_3_out_26, n8_bit_register_3_out_27,
       n8_bit_register_3_out_28, n8_bit_register_3_out_29, n8_bit_register_3_out_30,
       n8_bit_register_3_out_31, n8_bit_register_3_out_32, n8_bit_register_3_out_33,
       n8_bit_register_3_out_34, n8_bit_register_4_out_19, n8_bit_register_4_out_20,
       n8_bit_register_4_out_21, n8_bit_register_4_out_22, n8_bit_register_4_out_23,
       n8_bit_register_4_out_24, n8_bit_register_4_out_25, n8_bit_register_4_out_26,
       n8_bit_register_4_out_27, n8_bit_register_4_out_28, n8_bit_register_4_out_29,
       n8_bit_register_4_out_30, n8_bit_register_4_out_31, n8_bit_register_4_out_32,
       n8_bit_register_4_out_33, n8_bit_register_4_out_34, n8_bit_register_5_out_19,
       n8_bit_register_5_out_20, n8_bit_register_5_out_21, n8_bit_register_5_out_22,
       n8_bit_register_5_out_23, n8_bit_register_5_out_24, n8_bit_register_5_out_25,
       n8_bit_register_5_out_26, n8_bit_register_5_out_27, n8_bit_register_5_out_28,
       n8_bit_register_5_out_29, n8_bit_register_5_out_30, n8_bit_register_5_out_31,
       n8_bit_register_5_out_32, n8_bit_register_5_out_33, n8_bit_register_5_out_34,
       n8_bit_register_6_out_19, n8_bit_register_6_out_20, n8_bit_register_6_out_21,
       n8_bit_register_6_out_22, n8_bit_register_6_out_23, n8_bit_register_6_out_24,
       n8_bit_register_6_out_25, n8_bit_register_6_out_26, n8_bit_register_6_out_27,
       n8_bit_register_6_out_28, n8_bit_register_6_out_29, n8_bit_register_6_out_30,
       n8_bit_register_6_out_31, n8_bit_register_6_out_32, n8_bit_register_6_out_33,
       n8_bit_register_6_out_34, n8_bit_register_7_out_19, n8_bit_register_7_out_20,
       n8_bit_register_7_out_21, n8_bit_register_7_out_22, n8_bit_register_7_out_23,
       n8_bit_register_7_out_24, n8_bit_register_7_out_25, n8_bit_register_7_out_26,
       n8_bit_register_7_out_27, n8_bit_register_7_out_28, n8_bit_register_7_out_29,
       n8_bit_register_7_out_30, n8_bit_register_7_out_31, n8_bit_register_7_out_32,
       n8_bit_register_7_out_33, n8_bit_register_7_out_34, n8_bit_register_8_out_19,
       n8_bit_register_8_out_20, n8_bit_register_8_out_21, n8_bit_register_8_out_22,
       n8_bit_register_8_out_23, n8_bit_register_8_out_24, n8_bit_register_8_out_25, n8_bit_register_8_out_26;

  and and_1 (and_1_out, in_10, in_11);
  and and_2 (and_2_out, in_11, in_9);
  and and_3 (and_3_out, in_10, in_12);
  and and_4 (and_4_out, in_12, in_9);
  and and_5 (and_5_out, in_10, in_13);
  and and_6 (and_6_out, in_13, in_9);
  and and_7 (and_7_out, in_10, in_14);
  and and_8 (and_8_out, in_14, in_9);
  and and_9 (and_9_out, in_10, in_15);
  and and_10 (and_10_out, in_15, in_9);
  and and_11 (and_11_out, in_10, in_16);
  and and_12 (and_12_out, in_16, in_9);
  and and_13 (and_13_out, in_10, in_17);
  and and_14 (and_14_out, in_17, in_9);
  and and_15 (and_15_out, in_10, in_18);
  and and_16 (and_16_out, in_18, in_9);
  _8_Bit__Register u_8_bit_register_1 (
    .in_9(and_1_out), .in_10(and_2_out), .in_1(in_1), .out_19(out_19), .in_2(in_2), .out_20(out_20),
    .in_3(in_3), .out_21(out_21), .in_4(in_4), .out_22(out_22), .in_5(in_5), .out_23(out_23), .in_6(in_6),
    .out_24(out_24), .in_7(in_7), .out_25(out_25), .in_8(in_8), .out_26(out_26),
    .out_27(n8_bit_register_1_out_27), .out_28(n8_bit_register_1_out_28), .out_29(n8_bit_register_1_out_29),
    .out_30(n8_bit_register_1_out_30), .out_31(n8_bit_register_1_out_31), .out_32(n8_bit_register_1_out_32),
    .out_33(n8_bit_register_1_out_33), .out_34(n8_bit_register_1_out_34), .in_11(n8_bit_register_2_out_19),
    .in_12(n8_bit_register_2_out_20), .in_13(n8_bit_register_2_out_21), .in_14(n8_bit_register_2_out_22),
    .in_15(n8_bit_register_2_out_23), .in_16(n8_bit_register_2_out_24), .in_17(n8_bit_register_2_out_25),
    .in_18(n8_bit_register_2_out_26));
  _8_Bit__Register u_8_bit_register_2 (
    .in_9(and_3_out), .in_10(and_4_out), .in_1(n8_bit_register_1_out_27), .out_19(n8_bit_register_2_out_19),
    .in_2(n8_bit_register_1_out_28), .out_20(n8_bit_register_2_out_20), .in_3(n8_bit_register_1_out_29),
    .out_21(n8_bit_register_2_out_21), .in_4(n8_bit_register_1_out_30), .out_22(n8_bit_register_2_out_22),
    .in_5(n8_bit_register_1_out_31), .out_23(n8_bit_register_2_out_23), .in_6(n8_bit_register_1_out_32),
    .out_24(n8_bit_register_2_out_24), .in_7(n8_bit_register_1_out_33), .out_25(n8_bit_register_2_out_25),
    .in_8(n8_bit_register_1_out_34), .out_26(n8_bit_register_2_out_26), .out_27(n8_bit_register_2_out_27),
    .out_28(n8_bit_register_2_out_28), .out_29(n8_bit_register_2_out_29), .out_30(n8_bit_register_2_out_30),
    .out_31(n8_bit_register_2_out_31), .out_32(n8_bit_register_2_out_32), .out_33(n8_bit_register_2_out_33),
    .out_34(n8_bit_register_2_out_34), .in_11(n8_bit_register_3_out_19), .in_12(n8_bit_register_3_out_20),
    .in_13(n8_bit_register_3_out_21), .in_14(n8_bit_register_3_out_22), .in_15(n8_bit_register_3_out_23),
    .in_16(n8_bit_register_3_out_24), .in_17(n8_bit_register_3_out_25), .in_18(n8_bit_register_3_out_26));
  _8_Bit__Register u_8_bit_register_3 (
    .in_9(and_5_out), .in_10(and_6_out), .in_1(n8_bit_register_2_out_27), .out_19(n8_bit_register_3_out_19),
    .in_2(n8_bit_register_2_out_28), .out_20(n8_bit_register_3_out_20), .in_3(n8_bit_register_2_out_29),
    .out_21(n8_bit_register_3_out_21), .in_4(n8_bit_register_2_out_30), .out_22(n8_bit_register_3_out_22),
    .in_5(n8_bit_register_2_out_31), .out_23(n8_bit_register_3_out_23), .in_6(n8_bit_register_2_out_32),
    .out_24(n8_bit_register_3_out_24), .in_7(n8_bit_register_2_out_33), .out_25(n8_bit_register_3_out_25),
    .in_8(n8_bit_register_2_out_34), .out_26(n8_bit_register_3_out_26), .out_27(n8_bit_register_3_out_27),
    .out_28(n8_bit_register_3_out_28), .out_29(n8_bit_register_3_out_29), .out_30(n8_bit_register_3_out_30),
    .out_31(n8_bit_register_3_out_31), .out_32(n8_bit_register_3_out_32), .out_33(n8_bit_register_3_out_33),
    .out_34(n8_bit_register_3_out_34), .in_11(n8_bit_register_4_out_19), .in_12(n8_bit_register_4_out_20),
    .in_13(n8_bit_register_4_out_21), .in_14(n8_bit_register_4_out_22), .in_15(n8_bit_register_4_out_23),
    .in_16(n8_bit_register_4_out_24), .in_17(n8_bit_register_4_out_25), .in_18(n8_bit_register_4_out_26));
  _8_Bit__Register u_8_bit_register_4 (
    .in_9(and_7_out), .in_10(and_8_out), .in_1(n8_bit_register_3_out_27), .out_19(n8_bit_register_4_out_19),
    .in_2(n8_bit_register_3_out_28), .out_20(n8_bit_register_4_out_20), .in_3(n8_bit_register_3_out_29),
    .out_21(n8_bit_register_4_out_21), .in_4(n8_bit_register_3_out_30), .out_22(n8_bit_register_4_out_22),
    .in_5(n8_bit_register_3_out_31), .out_23(n8_bit_register_4_out_23), .in_6(n8_bit_register_3_out_32),
    .out_24(n8_bit_register_4_out_24), .in_7(n8_bit_register_3_out_33), .out_25(n8_bit_register_4_out_25),
    .in_8(n8_bit_register_3_out_34), .out_26(n8_bit_register_4_out_26), .out_27(n8_bit_register_4_out_27),
    .out_28(n8_bit_register_4_out_28), .out_29(n8_bit_register_4_out_29), .out_30(n8_bit_register_4_out_30),
    .out_31(n8_bit_register_4_out_31), .out_32(n8_bit_register_4_out_32), .out_33(n8_bit_register_4_out_33),
    .out_34(n8_bit_register_4_out_34), .in_11(n8_bit_register_5_out_19), .in_12(n8_bit_register_5_out_20),
    .in_13(n8_bit_register_5_out_21), .in_14(n8_bit_register_5_out_22), .in_15(n8_bit_register_5_out_23),
    .in_16(n8_bit_register_5_out_24), .in_17(n8_bit_register_5_out_25), .in_18(n8_bit_register_5_out_26));
  _8_Bit__Register u_8_bit_register_5 (
    .in_9(and_9_out), .in_10(and_10_out), .in_1(n8_bit_register_4_out_27), .out_19(n8_bit_register_5_out_19),
    .in_2(n8_bit_register_4_out_28), .out_20(n8_bit_register_5_out_20), .in_3(n8_bit_register_4_out_29),
    .out_21(n8_bit_register_5_out_21), .in_4(n8_bit_register_4_out_30), .out_22(n8_bit_register_5_out_22),
    .in_5(n8_bit_register_4_out_31), .out_23(n8_bit_register_5_out_23), .in_6(n8_bit_register_4_out_32),
    .out_24(n8_bit_register_5_out_24), .in_7(n8_bit_register_4_out_33), .out_25(n8_bit_register_5_out_25),
    .in_8(n8_bit_register_4_out_34), .out_26(n8_bit_register_5_out_26), .out_27(n8_bit_register_5_out_27),
    .out_28(n8_bit_register_5_out_28), .out_29(n8_bit_register_5_out_29), .out_30(n8_bit_register_5_out_30),
    .out_31(n8_bit_register_5_out_31), .out_32(n8_bit_register_5_out_32), .out_33(n8_bit_register_5_out_33),
    .out_34(n8_bit_register_5_out_34), .in_11(n8_bit_register_6_out_19), .in_12(n8_bit_register_6_out_20),
    .in_13(n8_bit_register_6_out_21), .in_14(n8_bit_register_6_out_22), .in_15(n8_bit_register_6_out_23),
    .in_16(n8_bit_register_6_out_24), .in_17(n8_bit_register_6_out_25), .in_18(n8_bit_register_6_out_26));
  _8_Bit__Register u_8_bit_register_6 (
    .in_9(and_11_out), .in_10(and_12_out), .in_1(n8_bit_register_5_out_27),
    .out_19(n8_bit_register_6_out_19), .in_2(n8_bit_register_5_out_28), .out_20(n8_bit_register_6_out_20),
    .in_3(n8_bit_register_5_out_29), .out_21(n8_bit_register_6_out_21), .in_4(n8_bit_register_5_out_30),
    .out_22(n8_bit_register_6_out_22), .in_5(n8_bit_register_5_out_31), .out_23(n8_bit_register_6_out_23),
    .in_6(n8_bit_register_5_out_32), .out_24(n8_bit_register_6_out_24), .in_7(n8_bit_register_5_out_33),
    .out_25(n8_bit_register_6_out_25), .in_8(n8_bit_register_5_out_34), .out_26(n8_bit_register_6_out_26),
    .out_27(n8_bit_register_6_out_27), .out_28(n8_bit_register_6_out_28), .out_29(n8_bit_register_6_out_29),
    .out_30(n8_bit_register_6_out_30), .out_31(n8_bit_register_6_out_31), .out_32(n8_bit_register_6_out_32),
    .out_33(n8_bit_register_6_out_33), .out_34(n8_bit_register_6_out_34), .in_11(n8_bit_register_7_out_19),
    .in_12(n8_bit_register_7_out_20), .in_13(n8_bit_register_7_out_21), .in_14(n8_bit_register_7_out_22),
    .in_15(n8_bit_register_7_out_23), .in_16(n8_bit_register_7_out_24), .in_17(n8_bit_register_7_out_25),
    .in_18(n8_bit_register_7_out_26));
  _8_Bit__Register u_8_bit_register_7 (
    .in_9(and_13_out), .in_10(and_14_out), .in_1(n8_bit_register_6_out_27),
    .out_19(n8_bit_register_7_out_19), .in_2(n8_bit_register_6_out_28), .out_20(n8_bit_register_7_out_20),
    .in_3(n8_bit_register_6_out_29), .out_21(n8_bit_register_7_out_21), .in_4(n8_bit_register_6_out_30),
    .out_22(n8_bit_register_7_out_22), .in_5(n8_bit_register_6_out_31), .out_23(n8_bit_register_7_out_23),
    .in_6(n8_bit_register_6_out_32), .out_24(n8_bit_register_7_out_24), .in_7(n8_bit_register_6_out_33),
    .out_25(n8_bit_register_7_out_25), .in_8(n8_bit_register_6_out_34), .out_26(n8_bit_register_7_out_26),
    .out_27(n8_bit_register_7_out_27), .out_28(n8_bit_register_7_out_28), .out_29(n8_bit_register_7_out_29),
    .out_30(n8_bit_register_7_out_30), .out_31(n8_bit_register_7_out_31), .out_32(n8_bit_register_7_out_32),
    .out_33(n8_bit_register_7_out_33), .out_34(n8_bit_register_7_out_34), .in_11(n8_bit_register_8_out_19),
    .in_12(n8_bit_register_8_out_20), .in_13(n8_bit_register_8_out_21), .in_14(n8_bit_register_8_out_22),
    .in_15(n8_bit_register_8_out_23), .in_16(n8_bit_register_8_out_24), .in_17(n8_bit_register_8_out_25),
    .in_18(n8_bit_register_8_out_26));
  _8_Bit__Register u_8_bit_register_8 (
    .in_9(and_15_out), .in_10(and_16_out), .in_1(n8_bit_register_7_out_27),
    .out_19(n8_bit_register_8_out_19), .in_2(n8_bit_register_7_out_28), .out_20(n8_bit_register_8_out_20),
    .in_3(n8_bit_register_7_out_29), .out_21(n8_bit_register_8_out_21), .in_4(n8_bit_register_7_out_30),
    .out_22(n8_bit_register_8_out_22), .in_5(n8_bit_register_7_out_31), .out_23(n8_bit_register_8_out_23),
    .in_6(n8_bit_register_7_out_32), .out_24(n8_bit_register_8_out_24), .in_7(n8_bit_register_7_out_33),
    .out_25(n8_bit_register_8_out_25), .in_8(n8_bit_register_7_out_34), .out_26(n8_bit_register_8_out_26),
    .in_11(button_1_out), .in_12(button_1_out), .in_13(button_1_out), .in_14(button_1_out),
    .in_15(button_1_out), .in_16(button_1_out), .in_17(button_1_out), .in_18(button_1_out));  // open: out_27, out_28, out_29, out_30, out_31, out_32, out_33, out_34
  Button button_1 (.out(button_1_out));
endmodule

module _8_Bit__Register (
  input  in_1,
  input  in_2,
  input  in_3,
  input  in_4,
  input  in_5,
  input  in_6,
  input  in_7,
  input  in_8,
  input  in_9,
  input  in_10,
  input  in_11,
  input  in_12,
  input  in_13,
  input  in_14,
  input  in_15,
  input  in_16,
  input  in_17,
  input  in_18,
  output out_19,
  output out_20,
  output out_21,
  output out_22,
  output out_23,
  output out_24,
  output out_25,
  output out_26,
  output out_27,
  output out_28,
  output out_29,
  output out_30,
  output out_31,
  output out_32,
  output out_33,
  output out_34
);

  wire sr_latch_1_out_4, sr_latch_2_out_4, sr_latch_3_out_4, sr_latch_4_out_4, sr_latch_5_out_4,
       sr_latch_6_out_4, sr_latch_7_out_4, sr_latch_8_out_4;

  SR_Latch sr_latch_1 (.write(in_1), .write_enable(in_10), .out_4(sr_latch_1_out_4), .read_enable(in_9));
  or or_1 (out_19, sr_latch_1_out_4, in_11);
  SR_Latch sr_latch_2 (.write(in_2), .write_enable(in_10), .out_4(sr_latch_2_out_4), .read_enable(in_9));
  or or_2 (out_20, sr_latch_2_out_4, in_12);
  SR_Latch sr_latch_3 (.write(in_3), .write_enable(in_10), .out_4(sr_latch_3_out_4), .read_enable(in_9));
  or or_3 (out_21, sr_latch_3_out_4, in_13);
  SR_Latch sr_latch_4 (.write(in_4), .write_enable(in_10), .out_4(sr_latch_4_out_4), .read_enable(in_9));
  or or_4 (out_22, sr_latch_4_out_4, in_14);
  SR_Latch sr_latch_5 (.write(in_5), .write_enable(in_10), .out_4(sr_latch_5_out_4), .read_enable(in_9));
  or or_5 (out_23, sr_latch_5_out_4, in_15);
  SR_Latch sr_latch_6 (.write(in_6), .write_enable(in_10), .out_4(sr_latch_6_out_4), .read_enable(in_9));
  or or_6 (out_24, sr_latch_6_out_4, in_16);
  SR_Latch sr_latch_7 (.write(in_7), .write_enable(in_10), .out_4(sr_latch_7_out_4), .read_enable(in_9));
  or or_7 (out_25, sr_latch_7_out_4, in_17);
  SR_Latch sr_latch_8 (.write(in_8), .write_enable(in_10), .out_4(sr_latch_8_out_4), .read_enable(in_9));
  or or_8 (out_26, sr_latch_8_out_4, in_18);

  assign out_27 = in_1;
  assign out_28 = in_2;
  assign out_29 = in_3;
  assign out_30 = in_4;
  assign out_31 = in_5;
  assign out_32 = in_6;
  assign out_33 = in_7;
  assign out_34 = in_8;
endmodule

module Bit__Matrix (
  input  in_1,
  input  in_2,
  input  in_3,
  input  in_4,
  input  in_5,
  input  in_6,
  input  in_7,
  input  in_8,
  input  in_9,
  input  in_10,
  input  in_11,
  input  in_12,
  input  in_13,
  input  in_14,
  input  in_15,
  output out_16
);

  wire and_1_out, and_2_out, and_3_out, and_4_out, and_5_out, and_6_out, and_7_out, and_8_out, and_9_out,
       and_10_out, and_11_out, and_12_out, and_13_out, and_14_out, and_15_out, and_16_out, and_17_out,
       and_18_out, and_19_out, and_20_out, and_21_out, and_22_out, and_23_out, and_24_out, and_25_out,
       and_26_out, and_27_out, and_28_out, and_29_out, and_30_out, and_31_out, and_32_out, and_33_out,
       and_34_out, and_35_out, and_36_out, and_37_out, and_38_out, and_39_out, and_40_out, and_41_out,
       and_42_out, and_43_out, and_44_out, and_45_out, and_46_out, and_47_out, and_48_out, and_49_out,
       and_50_out, and_51_out, and_52_out, and_53_out, and_54_out, and_55_out, and_56_out, and_57_out,
       and_58_out, and_59_out, and_60_out, and_61_out, and_62_out, and_63_out, and_64_out, or_1_out,
       or_2_out, or_3_out, or_4_out, or_5_out, or_6_out, or_7_out, or_8_out, or_9_out, or_10_out, or_11_out,
       or_12_out, or_13_out, or_14_out, or_15_out, or_16_out, or_17_out, or_18_out, or_19_out, or_20_out,
       or_21_out, or_22_out, or_23_out, or_24_out, or_25_out, or_26_out, or_27_out, or_28_out, or_29_out,
       or_30_out, or_31_out, or_32_out, or_34_out, or_35_out, sr_latch_1_out_4, sr_latch_2_out_4,
       sr_latch_3_out_4, sr_latch_4_out_4, sr_latch_5_out_4, sr_latch_6_out_4, sr_latch_7_out_4,
       sr_latch_8_out_4, sr_latch_9_out_4, sr_latch_10_out_4, sr_latch_11_out_4, sr_latch_12_out_4,
       sr_latch_13_out_4, sr_latch_14_out_4, sr_latch_15_out_4, sr_latch_16_out_4, sr_latch_17_out_4,
       sr_latch_18_out_4, sr_latch_19_out_4, sr_latch_20_out_4, sr_latch_21_out_4, sr_latch_22_out_4,
       sr_latch_23_out_4, sr_latch_24_out_4, sr_latch_25_out_4, sr_latch_26_out_4, sr_latch_27_out_4,
       sr_latch_28_out_4, sr_latch_29_out_4, sr_latch_30_out_4, sr_latch_31_out_4, sr_latch_32_out_4,
       undriven, undriven_2, undriven_3, undriven_4;

  and and_1 (and_1_out, in_11, in_12, in_2);
  SR_Latch sr_latch_1 (.write(in_10), .write_enable(and_2_out), .out_4(sr_latch_1_out_4), .read_enable(and_1_out));
  and and_2 (and_2_out, in_1, in_12, in_2);
  and and_3 (and_3_out, in_11, in_13, in_2);
  SR_Latch sr_latch_2 (.write(in_10), .write_enable(and_4_out), .out_4(sr_latch_2_out_4), .read_enable(and_3_out));
  and and_4 (and_4_out, in_1, in_13, in_2);
  and and_5 (and_5_out, in_11, in_14, in_2);
  SR_Latch sr_latch_3 (.write(in_10), .write_enable(and_6_out), .out_4(sr_latch_3_out_4), .read_enable(and_5_out));
  and and_6 (and_6_out, in_1, in_14, in_2);
  and and_7 (and_7_out, in_11, in_15, in_2);
  SR_Latch sr_latch_4 (.write(in_10), .write_enable(and_8_out), .out_4(sr_latch_4_out_4), .read_enable(and_7_out));
  and and_8 (and_8_out, in_1, in_15, in_2);
  or or_1 (or_1_out, undriven, sr_latch_1_out_4);
  and and_9 (and_9_out, in_1, in_12, in_3);
  or or_2 (or_2_out, undriven_2, sr_latch_2_out_4);
  and and_10 (and_10_out, in_1, in_13, in_3);
  or or_3 (or_3_out, undriven_3, sr_latch_3_out_4);
  and and_11 (and_11_out, in_1, in_14, in_3);
  or or_4 (or_4_out, undriven_4, sr_latch_4_out_4);
  and and_12 (and_12_out, in_1, in_15, in_3);
  and and_13 (and_13_out, in_11, in_12, in_3);
  or or_5 (or_5_out, or_1_out, sr_latch_5_out_4);
  SR_Latch sr_latch_5 (.write(in_10), .write_enable(and_9_out), .out_4(sr_latch_5_out_4), .read_enable(and_13_out));
  and and_14 (and_14_out, in_11, in_13, in_3);
  or or_6 (or_6_out, or_2_out, sr_latch_6_out_4);
  SR_Latch sr_latch_6 (.write(in_10), .write_enable(and_10_out), .out_4(sr_latch_6_out_4), .read_enable(and_14_out));
  and and_15 (and_15_out, in_11, in_14, in_3);
  or or_7 (or_7_out, or_3_out, sr_latch_7_out_4);
  SR_Latch sr_latch_7 (.write(in_10), .write_enable(and_11_out), .out_4(sr_latch_7_out_4), .read_enable(and_15_out));
  and and_16 (and_16_out, in_11, in_15, in_3);
  or or_8 (or_8_out, or_4_out, sr_latch_8_out_4);
  SR_Latch sr_latch_8 (.write(in_10), .write_enable(and_12_out), .out_4(sr_latch_8_out_4), .read_enable(and_16_out));
  and and_17 (and_17_out, in_11, in_12, in_1);
  and and_18 (and_18_out, in_1, in_12, in_1);
  and and_19 (and_19_out, in_11, in_13, in_1);
  and and_20 (and_20_out, in_1, in_13, in_1);
  and and_21 (and_21_out, in_11, in_14, in_1);
  and and_22 (and_22_out, in_1, in_14, in_1);
  and and_23 (and_23_out, in_11, in_15, in_1);
  and and_24 (and_24_out, in_1, in_15, in_1);
  or or_9 (or_9_out, or_5_out, sr_latch_9_out_4);
  SR_Latch sr_latch_9 (.write(in_10), .write_enable(and_18_out), .out_4(sr_latch_9_out_4), .read_enable(and_17_out));
  or or_10 (or_10_out, or_6_out, sr_latch_10_out_4);
  SR_Latch sr_latch_10 (.write(in_10), .write_enable(and_20_out), .out_4(sr_latch_10_out_4), .read_enable(and_19_out));
  or or_11 (or_11_out, or_7_out, sr_latch_11_out_4);
  SR_Latch sr_latch_11 (.write(in_10), .write_enable(and_22_out), .out_4(sr_latch_11_out_4), .read_enable(and_21_out));
  or or_12 (or_12_out, or_8_out, sr_latch_12_out_4);
  SR_Latch sr_latch_12 (.write(in_10), .write_enable(and_24_out), .out_4(sr_latch_12_out_4), .read_enable(and_23_out));
  and and_25 (and_25_out, in_11, in_12, in_5);
  SR_Latch sr_latch_13 (.write(in_10), .write_enable(and_26_out), .out_4(sr_latch_13_out_4), .read_enable(and_25_out));
  and and_26 (and_26_out, in_1, in_12, in_5);
  and and_27 (and_27_out, in_11, in_13, in_5);
  SR_Latch sr_latch_14 (.write(in_10), .write_enable(and_28_out), .out_4(sr_latch_14_out_4), .read_enable(and_27_out));
  and and_28 (and_28_out, in_1, in_13, in_5);
  and and_29 (and_29_out, in_11, in_14, in_5);
  SR_Latch sr_latch_15 (.write(in_10), .write_enable(and_30_out), .out_4(sr_latch_15_out_4), .read_enable(and_29_out));
  and and_30 (and_30_out, in_1, in_14, in_5);
  and and_31 (and_31_out, in_11, in_15, in_5);
  SR_Latch sr_latch_16 (.write(in_10), .write_enable(and_32_out), .out_4(sr_latch_16_out_4), .read_enable(and_31_out));
  and and_32 (and_32_out, in_1, in_15, in_5);
  or or_13 (or_13_out, or_9_out, sr_latch_13_out_4);
  or or_14 (or_14_out, or_10_out, sr_latch_14_out_4);
  or or_15 (or_15_out, or_11_out, sr_latch_15_out_4);
  or or_16 (or_16_out, or_12_out, sr_latch_16_out_4);
  and and_33 (and_33_out, in_11, in_12, in_6);
  SR_Latch sr_latch_17 (.write(in_10), .write_enable(and_34_out), .out_4(sr_latch_17_out_4), .read_enable(and_33_out));
  and and_34 (and_34_out, in_1, in_12, in_6);
  and and_35 (and_35_out, in_11, in_13, in_6);
  SR_Latch sr_latch_18 (.write(in_10), .write_enable(and_36_out), .out_4(sr_latch_18_out_4), .read_enable(and_35_out));
  and and_36 (and_36_out, in_1, in_13, in_6);
  and and_37 (and_37_out, in_11, in_14, in_6);
  SR_Latch sr_latch_19 (.write(in_10), .write_enable(and_38_out), .out_4(sr_latch_19_out_4), .read_enable(and_37_out));
  and and_38 (and_38_out, in_1, in_14, in_6);
  and and_39 (and_39_out, in_11, in_15, in_6);
  SR_Latch sr_latch_20 (.write(in_10), .write_enable(and_40_out), .out_4(sr_latch_20_out_4), .read_enable(and_39_out));
  and and_40 (and_40_out, in_1, in_15, in_6);
  or or_17 (or_17_out, or_13_out, sr_latch_17_out_4);
  and and_41 (and_41_out, in_1, in_12, in_7);
  or or_18 (or_18_out, or_14_out, sr_latch_18_out_4);
  and and_42 (and_42_out, in_1, in_13, in_7);
  or or_19 (or_19_out, or_15_out, sr_latch_19_out_4);
  and and_43 (and_43_out, in_1, in_14, in_7);
  or or_20 (or_20_out, or_16_out, sr_latch_20_out_4);
  and and_44 (and_44_out, in_1, in_15, in_7);
  and and_45 (and_45_out, in_11, in_12, in_7);
  or or_21 (or_21_out, or_17_out, sr_latch_21_out_4);
  SR_Latch sr_latch_21 (.write(in_10), .write_enable(and_41_out), .out_4(sr_latch_21_out_4), .read_enable(and_45_out));
  and and_46 (and_46_out, in_11, in_13, in_7);
  or or_22 (or_22_out, or_18_out, sr_latch_22_out_4);
  SR_Latch sr_latch_22 (.write(in_10), .write_enable(and_42_out), .out_4(sr_latch_22_out_4), .read_enable(and_46_out));
  and and_47 (and_47_out, in_11, in_14, in_7);
  or or_23 (or_23_out, or_19_out, sr_latch_23_out_4);
  SR_Latch sr_latch_23 (.write(in_10), .write_enable(and_43_out), .out_4(sr_latch_23_out_4), .read_enable(and_47_out));
  and and_48 (and_48_out, in_11, in_15, in_7);
  or or_24 (or_24_out, or_20_out, sr_latch_24_out_4);
  SR_Latch sr_latch_24 (.write(in_10), .write_enable(and_44_out), .out_4(sr_latch_24_out_4), .read_enable(and_48_out));
  and and_49 (and_49_out, in_11, in_12, in_8);
  and and_50 (and_50_out, in_1, in_12, in_8);
  and and_51 (and_51_out, in_11, in_13, in_8);
  and and_52 (and_52_out, in_1, in_13, in_8);
  and and_53 (and_53_out, in_11, in_14, in_8);
  and and_54 (and_54_out, in_1, in_14, in_8);
  and and_55 (and_55_out, in_11, in_15, in_8);
  and and_56 (and_56_out, in_1, in_15, in_8);
  or or_25 (or_25_out, or_21_out, sr_latch_25_out_4);
  SR_Latch sr_latch_25 (.write(in_10), .write_enable(and_50_out), .out_4(sr_latch_25_out_4), .read_enable(and_49_out));
  or or_26 (or_26_out, or_22_out, sr_latch_26_out_4);
  SR_Latch sr_latch_26 (.write(in_10), .write_enable(and_52_out), .out_4(sr_latch_26_out_4), .read_enable(and_51_out));
  or or_27 (or_27_out, or_23_out, sr_latch_27_out_4);
  SR_Latch sr_latch_27 (.write(in_10), .write_enable(and_54_out), .out_4(sr_latch_27_out_4), .read_enable(and_53_out));
  or or_28 (or_28_out, or_24_out, sr_latch_28_out_4);
  SR_Latch sr_latch_28 (.write(in_10), .write_enable(and_56_out), .out_4(sr_latch_28_out_4), .read_enable(and_55_out));
  and and_57 (and_57_out, in_11, in_12, in_9);
  SR_Latch sr_latch_29 (.write(in_10), .write_enable(and_58_out), .out_4(sr_latch_29_out_4), .read_enable(and_57_out));
  and and_58 (and_58_out, in_1, in_12, in_9);
  and and_59 (and_59_out, in_11, in_13, in_9);
  SR_Latch sr_latch_30 (.write(in_10), .write_enable(and_60_out), .out_4(sr_latch_30_out_4), .read_enable(and_59_out));
  and and_60 (and_60_out, in_1, in_13, in_9);
  and and_61 (and_61_out, in_11, in_14, in_9);
  SR_Latch sr_latch_31 (.write(in_10), .write_enable(and_62_out), .out_4(sr_latch_31_out_4), .read_enable(and_61_out));
  and and_62 (and_62_out, in_1, in_14, in_9);
  and and_63 (and_63_out, in_11, in_15, in_9);
  SR_Latch sr_latch_32 (.write(in_10), .write_enable(and_64_out), .out_4(sr_latch_32_out_4), .read_enable(and_63_out));
  and and_64 (and_64_out, in_1, in_15, in_9);
  or or_29 (or_29_out, or_25_out, sr_latch_29_out_4);
  or or_30 (or_30_out, or_26_out, sr_latch_30_out_4);
  or or_31 (or_31_out, or_27_out, sr_latch_31_out_4);
  or or_32 (or_32_out, or_28_out, sr_latch_32_out_4);
  or or_33 (out_16, or_29_out, or_34_out);
  or or_34 (or_34_out, or_30_out, or_35_out);
  or or_35 (or_35_out, or_31_out, or_32_out);

  assign in_4 = in_1;
endmodule

module _8bitoverride (
  input  in_1,
  input  in_2,
  input  in_3,
  input  in_4,
  input  in_5,
  input  in_6,
  input  in_7,
  input  in_8,
  input  in_9,
  input  in_10,
  input  in_11,
  input  in_12,
  input  in_13,
  input  in_14,
  input  in_15,
  input  in_16,
  output out_17,
  output out_18
);

  wire and_1_out, and_2_out, and_3_out, and_4_out, and_5_out, and_6_out, and_7_out, and_8_out, and_9_out,
       and_10_out, and_11_out, and_12_out, and_13_out, and_14_out, not_1_out, not_2_out, not_3_out,
       not_4_out, not_5_out, not_6_out, not_7_out, not_8_out, not_9_out, not_10_out, not_11_out, not_12_out,
       not_13_out, not_14_out, or_1_out, or_2_out, or_3_out, or_4_out, or_5_out, or_6_out, or_7_out,
       or_8_out, or_9_out, or_10_out, or_11_out, or_12_out, undriven;

  not not_1 (not_1_out, in_16);
  not not_2 (not_2_out, in_15);
  or or_1 (or_1_out, in_14, in_16);
  or or_2 (or_2_out, in_15, in_13);
  and and_1 (and_1_out, in_13, not_1_out);
  and and_2 (and_2_out, in_14, not_2_out);
  not not_3 (not_3_out, or_3_out);
  or or_3 (or_3_out, in_12, or_1_out);
  or or_4 (or_4_out, undriven, or_2_out);
  not not_4 (not_4_out, or_4_out);
  and and_3 (and_3_out, undriven, not_5_out);
  not not_5 (not_5_out, or_1_out);
  and and_4 (and_4_out, in_12, not_6_out);
  not not_6 (not_6_out, or_2_out);
  or or_5 (or_5_out, in_8, or_7_out);
  or or_6 (or_6_out, in_7, or_8_out);
  or or_7 (or_7_out, in_10, or_3_out);
  not not_7 (not_7_out, or_7_out);
  not not_8 (not_8_out, or_8_out);
  or or_8 (or_8_out, in_9, or_4_out);
  and and_5 (and_5_out, in_9, not_3_out);
  and and_6 (and_6_out, in_10, not_4_out);
  or or_9 (or_9_out, in_4, or_10_out);
  or or_10 (or_10_out, in_6, or_5_out);
  not not_9 (not_9_out, or_10_out);
  not not_10 (not_10_out, or_11_out);
  or or_11 (or_11_out, in_5, or_6_out);
  and and_7 (and_7_out, in_5, not_11_out);
  not not_11 (not_11_out, or_5_out);
  and and_8 (and_8_out, in_6, not_12_out);
  not not_12 (not_12_out, or_6_out);
  and and_9 (and_9_out, in_7, not_7_out);
  and and_10 (and_10_out, in_8, not_8_out);
  and and_11 (and_11_out, in_1, not_13_out);
  not not_13 (not_13_out, or_9_out);
  not not_14 (not_14_out, or_12_out);
  or or_12 (or_12_out, in_3, or_11_out);
  and and_12 (and_12_out, in_3, not_9_out);
  and and_13 (and_13_out, in_4, not_10_out);
  and and_14 (and_14_out, in_2, not_14_out);
  or or_13 (out_17, and_11_out, and_12_out, and_7_out, and_9_out, and_5_out, and_3_out, and_1_out, in_15);
  or or_14 (out_18, and_14_out, and_13_out, and_8_out, and_10_out, and_6_out, and_4_out, and_2_out, in_16);
endmodule

module override (
  input  in_1,
  input  in_2,
  output out_3,
  output out_4
);

  wire not_1_out, not_2_out;

  not not_1 (not_1_out, in_2);
  and and_1 (out_3, in_1, not_1_out);
  and and_2 (out_4, not_2_out, in_2);
  not not_2 (not_2_out, in_1);
endmodule

module SR_Latch (
  input  write,
  input  read_enable,
  input  write_enable,
  output out_4
);

  wire and_1_out, and_2_out, nand_1_out, or_1_out;

  or or_1 (or_1_out, and_2_out, and_1_out);
  and and_1 (and_1_out, write, write_enable);
  nand nand_1 (nand_1_out, ~write, write_enable);  // NAND_Gate
  and and_2 (and_2_out, or_1_out, nand_1_out);
  and and_3 (out_4, and_2_out, read_enable);
endmodule

module HA (
  input  in_1,
  input  in_2,
  output out_3,
  output out_4
);

  xor xor_1 (out_3, in_1, in_2);
  and and_1 (out_4, in_1, in_2);
endmodule

module VA (
  input  in_1,
  input  in_2,
  input  in_3,
  output out_4,
  output out_5
);

  wire and_1_out, xnor_1_out;

  xor xor_1 (out_4, in_1, in_2, in_3);
  xnor xnor_1 (xnor_1_out, in_2, in_1, in_3);
  and and_1 (and_1_out, ~in_3, ~in_2, ~in_1);  // AND_Gate
  and and_2 (out_5, xnor_1_out, ~and_1_out);  // AND_Gate
endmodule
