// Logisim project logisch!.circ as structural Verilog: 6 circuits, main circuit main
module main (
  input  in_1,
  input  in_2,
  input  in_3,
  input  in_4,
  input  A,
  input  B,
  input  MC_Switch,
  input  DC_Switch,
  input  IO,
  input  in_10,
  input  in_11,
  input  in_12,
  input  in_13,
  output out_14
);

  wire demultiplexer_1_out0, demultiplexer_1_out1, multiplexer_1_out;
  wire [3:0] joystick_1_x, joystick_1_y, undriven;

  _7_Segment_Display u_7_segment_display_1 (
    .g(in_1), .f(in_2), .a(in_3), .b(in_4), .e(in_13), .d(in_12), .c(in_11), .dp(in_10));
  Joystick joystick_1 (.x(joystick_1_x), .y(joystick_1_y));
  Clock clock_1 (.out(out_14));
  Hex_Digit_Display hex_digit_display_1 (.value(undriven));  // open: dp
  RAM ram_1 ();  // open: addr, data, sel, clk, ld, clr
  ALU alu_1 ();
  Multiplexer multiplexer_1 (.in0(A), .in1(B), .out(multiplexer_1_out), .sel(MC_Switch), .en(IO));
  Demultiplexer demultiplexer_1 (
    .out0(demultiplexer_1_out0), .out1(demultiplexer_1_out1), .in(multiplexer_1_out), .sel(DC_Switch), .en(IO));
endmodule

module ALU (
);

  ADD add_1 ();  // open: in_1, in_2, in_3, in_4, in_5, in_6, in_7, in_8, in_9, in_10, in_11, in_12, in_13, in_14, in_15, in_16
endmodule

module ADD (
  input  in_1,
  input  in_2,
  input  in_3,
  input  in_4,
  input  in_5,
  input  in_6,
  input  in_7,
  input  in_8,
  input  in_9,
  input  in_10,
  input  in_11,
  input  in_12,
  input  in_13,
  input  in_14,
  input  in_15,
  input  in_16
);

  LED led_1 (.in(in_4));
endmodule

module COMP (
  input  in_1,
  input  in_2,
  input  in_3,
  input  in_4,
  input  in_5,
  input  in_6,
  input  in_7,
  input  in_8,
  input  in_9,
  input  in_10,
  input  in_11,
  input  in_12,
  input  in_13,
  input  in_14,
  input  in_15,
  input  in_16
);

  wire bitcomp_8_out_3, bitcomp_8_out_4;

  BITCOMP bitcomp_1 (.in_1(in_1), .in_2(in_2));  // open: out_3, out_4
  BITCOMP bitcomp_2 (.in_1(in_3), .in_2(in_4));  // open: out_3, out_4
  BITCOMP bitcomp_3 (.in_1(in_5), .in_2(in_6));  // open: out_3, out_4
  BITCOMP bitcomp_4 (.in_1(in_7), .in_2(in_8));  // open: out_3, out_4
  BITCOMP bitcomp_5 (.in_1(in_9), .in_2(in_10));  // open: out_3, out_4
  BITCOMP bitcomp_6 (.in_1(in_11), .in_2(in_12));  // open: out_3, out_4
  BITCOMP bitcomp_7 (.in_1(in_13), .in_2(in_14));  // open: out_3, out_4
  BITCOMP bitcomp_8 (.in_1(in_15), .in_2(in_16), .out_3(bitcomp_8_out_3), .out_4(bitcomp_8_out_4));
endmodule

module BITCOMP (
  input  in_1,
  input  in_2,
  output out_3,
  output out_4
);

  wire xor_1_out;

  xor xor_1 (xor_1_out, in_1, in_2);
  and and_1 (out_3, in_1, xor_1_out);
  and and_2 (out_4, xor_1_out, in_2);
endmodule

module override (
  input  in_1,
  input  in_2,
  output out_3,
  output out_4
);

  wire not_1_out, not_2_out;

  not not_1 (not_1_out, in_2);
  and and_1 (out_3, in_1, not_1_out);
  and and_2 (out_4, not_2_out, in_2);
  not not_2 (not_2_out, in_1);
endmodule
