// Logisim project logisch.circ as structural Verilog
module main (
  input  [7:0] in_1,
  input  [7:0] in_2,
  input  in_3,
  input  in_4,
  input  in_5,
  input  in_6,
  input  A,
  input  in_8,
  input  B,
  input  MC_Switch,
  input  DC_Switch,
  input  in_12,
  input  IO,
  input  in_14,
  output [7:0] out_15,
  output [7:0] out_16,
  output out_17
);

  wire demultiplexer_1_out0, demultiplexer_1_out1, multiplexer_1_out,
       sieben_segment_controller_dezimal_1_out_6, sieben_segment_controller_dezimal_1_out_7,
       sieben_segment_controller_dezimal_1_out_8, sieben_segment_controller_dezimal_1_out_9,
       sieben_segment_controller_dezimal_1_out_10, sieben_segment_controller_dezimal_1_out_11,
       sieben_segment_controller_dezimal_1_out_12, sieben_segment_controller_dezimal_1_out_13;

  _7_Segment_Display u_7_segment_display_1 (
    .g(sieben_segment_controller_dezimal_1_out_6), .f(sieben_segment_controller_dezimal_1_out_7),
    .a(sieben_segment_controller_dezimal_1_out_8), .b(sieben_segment_controller_dezimal_1_out_9),
    .e(sieben_segment_controller_dezimal_1_out_10), .d(sieben_segment_controller_dezimal_1_out_11),
    .c(sieben_segment_controller_dezimal_1_out_12), .dp(sieben_segment_controller_dezimal_1_out_13));
  Sieben_Segment_Controller_Dezimal sieben_segment_controller_dezimal_1 (
    .in_1(in_3), .in_2(in_4), .in_3(in_5), .in_4(in_6), .in_5(in_8),
    .out_10(sieben_segment_controller_dezimal_1_out_10), .out_11(sieben_segment_controller_dezimal_1_out_11),
    .out_12(sieben_segment_controller_dezimal_1_out_12), .out_13(sieben_segment_controller_dezimal_1_out_13),
    .out_6(sieben_segment_controller_dezimal_1_out_6), .out_7(sieben_segment_controller_dezimal_1_out_7),
    .out_8(sieben_segment_controller_dezimal_1_out_8), .out_9(sieben_segment_controller_dezimal_1_out_9));
  ALU alu_1 (.in_4(in_12), .in_3(in_14), .OUT(out_15), .A(in_2), .B(in_1), .FLAG(out_17), .L_8FLAG(out_16));
  Multiplexer multiplexer_1 (.in0(A), .in1(B), .out(multiplexer_1_out), .sel(MC_Switch), .en(IO));
  Demultiplexer demultiplexer_1 (
    .out0(demultiplexer_1_out0), .out1(demultiplexer_1_out1), .in(multiplexer_1_out), .sel(DC_Switch), .en(IO));
endmodule

module ALU (
  input  [7:0] A,
  input  [7:0] B,
  input  in_3,
  input  in_4,
  output [7:0] OUT,
  output [7:0] L_8FLAG,
  output FLAG
);

  wire add_1_out_4, and_1_out, and_2_out, and_3_out, and_4_out;
  wire [1:0] comp_1_a___b;
  wire [7:0] add_1_out_3, l_8_bit_mux_c01a6ef4_2_out_5, l_8x1bitand_f58f873e_1_out_3,
       l_8x1bitand_f58f873e_2_out_3, l_8x1bitand_f58f873e_3_out_3, l_8x1bitand_f58f873e_4_out_3,
       l_8x1bitand_f58f873e_5_out_3, l_8x1bitand_f58f873e_6_out_3, l_8x1bitand_f58f873e_7_out_3,
       l_8x1bitand_f58f873e_8_out_3;
  wire [15:0] mul_1_out_3;

  and and_1 (and_1_out, ~in_3, ~in_4);  // AND_Gate
  and and_2 (and_2_out, in_3, ~in_4);  // AND_Gate
  and and_3 (and_3_out, ~in_3, in_4);  // AND_Gate
  and and_4 (and_4_out, in_3, in_4);
  L_8x1bitAND_f58f873e l_8x1bitand_f58f873e_1 (.in_1(B), .out_3(l_8x1bitand_f58f873e_1_out_3), .in_2(and_1_out));
  L_8x1bitAND_f58f873e l_8x1bitand_f58f873e_2 (.in_1(A), .out_3(l_8x1bitand_f58f873e_2_out_3), .in_2(and_1_out));
  L_8x1bitAND_f58f873e l_8x1bitand_f58f873e_3 (.in_1(B), .out_3(l_8x1bitand_f58f873e_3_out_3), .in_2(and_2_out));
  L_8x1bitAND_f58f873e l_8x1bitand_f58f873e_4 (.in_1(A), .out_3(l_8x1bitand_f58f873e_4_out_3), .in_2(and_2_out));
  L_8x1bitAND_f58f873e l_8x1bitand_f58f873e_5 (.in_1(B), .out_3(l_8x1bitand_f58f873e_5_out_3), .in_2(and_3_out));
  L_8x1bitAND_f58f873e l_8x1bitand_f58f873e_6 (.in_1(A), .out_3(l_8x1bitand_f58f873e_6_out_3), .in_2(and_3_out));
  L_8x1bitAND_f58f873e l_8x1bitand_f58f873e_7 (.in_1(B), .out_3(l_8x1bitand_f58f873e_7_out_3), .in_2(and_4_out));
  L_8x1bitAND_f58f873e l_8x1bitand_f58f873e_8 (.in_1(A), .out_3(l_8x1bitand_f58f873e_8_out_3), .in_2(and_4_out));
  ADD add_1 (
    .out_4(add_1_out_4), .in_1(l_8x1bitand_f58f873e_1_out_3), .in_2(l_8x1bitand_f58f873e_2_out_3),
    .out_3(add_1_out_3));
  MUL mul_1 (.in_1(l_8x1bitand_f58f873e_3_out_3), .in_2(l_8x1bitand_f58f873e_4_out_3), .out_3(mul_1_out_3));
  COMP comp_1 (
    .A___B(comp_1_a___b[0]), .B___A(comp_1_a___b[1]), .in_1(l_8x1bitand_f58f873e_5_out_3),
    .B(l_8x1bitand_f58f873e_6_out_3));
  L_8_Bit_MUX_c01a6ef4 l_8_bit_mux_c01a6ef4_1 (
    .in_1(l_8_bit_mux_c01a6ef4_2_out_5), .in_2({8{1'b0}}), .out_5(OUT), .in_3(in_4));  // open: out_4
  L_8_Bit_MUX_c01a6ef4 l_8_bit_mux_c01a6ef4_2 (
    .in_1(add_1_out_3), .in_2(mul_1_out_3[7:0]), .out_5(l_8_bit_mux_c01a6ef4_2_out_5), .in_3(in_3));  // open: out_4
  L_8_Bit_MUX_c01a6ef4 l_8_bit_mux_c01a6ef4_3 (
    .in_1(mul_1_out_3[15:8]), .in_2({{6{1'b0}}, comp_1_a___b}), .out_5(L_8FLAG), .in_3(in_4));  // open: out_4
  L_bit_MUX_72b0574c l_bit_mux_72b0574c_1 (.in_1(add_1_out_4), .in_2(1'b0), .out_5(FLAG), .in_3(in_4));  // open: out_4
endmodule

module ADD (
  input  [7:0] in_1,
  input  [7:0] in_2,
  output [7:0] out_3,
  output out_4
);

  wire ha_1_out_4, va_1_out_5, va_2_out_5, va_3_out_5, va_4_out_5, va_5_out_5, va_6_out_5;

  HA ha_1 (.in_1(in_1[0]), .in_2(in_2[0]), .out_3(out_3[0]), .out_4(ha_1_out_4));
  VA va_1 (.in_1(in_1[1]), .in_2(in_2[1]), .in_3(ha_1_out_4), .out_4(out_3[1]), .out_5(va_1_out_5));
  VA va_2 (.in_1(in_1[2]), .in_2(in_2[2]), .in_3(va_1_out_5), .out_4(out_3[2]), .out_5(va_2_out_5));
  VA va_3 (.in_1(in_1[3]), .in_2(in_2[3]), .in_3(va_2_out_5), .out_4(out_3[3]), .out_5(va_3_out_5));
  VA va_4 (.in_1(in_1[4]), .in_2(in_2[4]), .in_3(va_3_out_5), .out_4(out_3[4]), .out_5(va_4_out_5));
  VA va_5 (.in_1(in_1[5]), .in_2(in_2[5]), .in_3(va_4_out_5), .out_4(out_3[5]), .out_5(va_5_out_5));
  VA va_6 (.in_1(in_1[6]), .in_2(in_2[6]), .in_3(va_5_out_5), .out_4(out_3[6]), .out_5(va_6_out_5));
  VA va_7 (.in_1(in_1[7]), .in_2(in_2[7]), .in_3(va_6_out_5), .out_4(out_3[7]), .out_5(out_4));
endmodule

module SUB (
  input  [7:0] in_1,
  input  [7:0] B,
  output [7:0] out_3,
  output out_4
);

  COMP comp_1 (.in_1(in_1), .B(B));  // open: A___B, B___A

  // Notes on the sheet:
  //   A
  //   /
endmodule

module MUL (
  input  [7:0] in_1,
  input  [7:0] in_2,
  output [15:0] out_3
);

  wire [7:0] l_8x1bitand_f58f873e_1_out_3, l_8x1bitand_f58f873e_2_out_3, l_8x1bitand_f58f873e_3_out_3,
       l_8x1bitand_f58f873e_4_out_3, l_8x1bitand_f58f873e_5_out_3, l_8x1bitand_f58f873e_6_out_3,
       l_8x1bitand_f58f873e_8_out_3;
  wire [7:1] add_1_out_3, add_2_out_3, add_3_out_3, add_4_out_3, add_5_out_3, add_6_out_3,
       l_8x1bitand_f58f873e_7_out_3;
  wire [7:7] add_1_out_4, add_2_out_4, add_3_out_4, add_4_out_4, add_5_out_4, add_6_out_4;

  L_8x1bitAND_f58f873e l_8x1bitand_f58f873e_1 (.in_1(in_2), .out_3(l_8x1bitand_f58f873e_1_out_3), .in_2(in_1[6]));
  L_8x1bitAND_f58f873e l_8x1bitand_f58f873e_2 (.in_1(in_2), .out_3(l_8x1bitand_f58f873e_2_out_3), .in_2(in_1[7]));
  L_8x1bitAND_f58f873e l_8x1bitand_f58f873e_3 (.in_1(in_2), .out_3(l_8x1bitand_f58f873e_3_out_3), .in_2(in_1[4]));
  L_8x1bitAND_f58f873e l_8x1bitand_f58f873e_4 (.in_1(in_2), .out_3(l_8x1bitand_f58f873e_4_out_3), .in_2(in_1[5]));
  L_8x1bitAND_f58f873e l_8x1bitand_f58f873e_5 (.in_1(in_2), .out_3(l_8x1bitand_f58f873e_5_out_3), .in_2(in_1[2]));
  L_8x1bitAND_f58f873e l_8x1bitand_f58f873e_6 (.in_1(in_2), .out_3(l_8x1bitand_f58f873e_6_out_3), .in_2(in_1[3]));
  L_8x1bitAND_f58f873e l_8x1bitand_f58f873e_7 (
    .in_1(in_2), .out_3({l_8x1bitand_f58f873e_7_out_3, out_3[0]}), .in_2(in_1[0]));
  L_8x1bitAND_f58f873e l_8x1bitand_f58f873e_8 (.in_1(in_2), .out_3(l_8x1bitand_f58f873e_8_out_3), .in_2(in_1[1]));
  ADD add_1 (
    .out_4(add_1_out_4[7]), .in_1({1'b0, l_8x1bitand_f58f873e_7_out_3}), .in_2(l_8x1bitand_f58f873e_8_out_3),
    .out_3({add_1_out_3, out_3[1]}));
  ADD add_2 (
    .out_4(add_2_out_4[7]), .in_1({add_1_out_4[7], add_1_out_3}), .in_2(l_8x1bitand_f58f873e_5_out_3),
    .out_3({add_2_out_3, out_3[2]}));
  ADD add_3 (
    .out_4(add_3_out_4[7]), .in_1({add_2_out_4[7], add_2_out_3}), .in_2(l_8x1bitand_f58f873e_6_out_3),
    .out_3({add_3_out_3, out_3[3]}));
  ADD add_4 (
    .out_4(add_4_out_4[7]), .in_1({add_3_out_4[7], add_3_out_3}), .in_2(l_8x1bitand_f58f873e_3_out_3),
    .out_3({add_4_out_3, out_3[4]}));
  ADD add_5 (
    .out_4(add_5_out_4[7]), .in_1({add_4_out_4[7], add_4_out_3}), .in_2(l_8x1bitand_f58f873e_4_out_3),
    .out_3({add_5_out_3, out_3[5]}));
  ADD add_6 (
    .out_4(add_6_out_4[7]), .in_1({add_5_out_4[7], add_5_out_3}), .in_2(l_8x1bitand_f58f873e_1_out_3),
    .out_3({add_6_out_3, out_3[6]}));
  ADD add_7 (
    .out_4(out_3[15]), .in_1({add_6_out_4[7], add_6_out_3}), .in_2(l_8x1bitand_f58f873e_2_out_3),
    .out_3(out_3[14:7]));
endmodule

module DIV (
  input  [7:0] in_1,
  input  [7:0] in_2
);
endmodule

module COMP (
  input  [7:0] in_1,
  input  [7:0] B,
  output A___B,
  output B___A
);

  wire bitcomp_1_out_3, bitcomp_1_out_4, bitcomp_2_out_3, bitcomp_2_out_4, bitcomp_3_out_3, bitcomp_3_out_4,
       bitcomp_4_out_3, bitcomp_4_out_4, bitcomp_5_out_3, bitcomp_5_out_4, bitcomp_6_out_3, bitcomp_6_out_4,
       bitcomp_7_out_3, bitcomp_7_out_4, bitcomp_8_out_3, bitcomp_8_out_4;

  BITCOMP bitcomp_1 (.in_1(in_1[0]), .in_2(B[0]), .out_3(bitcomp_1_out_3), .out_4(bitcomp_1_out_4));
  BITCOMP bitcomp_2 (.in_1(in_1[1]), .in_2(B[1]), .out_3(bitcomp_2_out_3), .out_4(bitcomp_2_out_4));
  BITCOMP bitcomp_3 (.in_1(in_1[2]), .in_2(B[2]), .out_3(bitcomp_3_out_3), .out_4(bitcomp_3_out_4));
  BITCOMP bitcomp_4 (.in_1(in_1[3]), .in_2(B[3]), .out_3(bitcomp_4_out_3), .out_4(bitcomp_4_out_4));
  BITCOMP bitcomp_5 (.in_1(in_1[4]), .in_2(B[4]), .out_3(bitcomp_5_out_3), .out_4(bitcomp_5_out_4));
  BITCOMP bitcomp_6 (.in_1(in_1[5]), .in_2(B[5]), .out_3(bitcomp_6_out_3), .out_4(bitcomp_6_out_4));
  BITCOMP bitcomp_7 (.in_1(in_1[6]), .in_2(B[6]), .out_3(bitcomp_7_out_3), .out_4(bitcomp_7_out_4));
  BITCOMP bitcomp_8 (.in_1(in_1[7]), .in_2(B[7]), .out_3(bitcomp_8_out_3), .out_4(bitcomp_8_out_4));
  L_8bitoverride_e8d84573 l_8bitoverride_e8d84573_1 (
    .in_1(bitcomp_1_out_3), .in_2(bitcomp_1_out_4), .in_3(bitcomp_2_out_3), .in_4(bitcomp_2_out_4),
    .in_5(bitcomp_3_out_3), .in_6(bitcomp_3_out_4), .in_7(bitcomp_4_out_3), .in_8(bitcomp_4_out_4),
    .in_9(bitcomp_5_out_3), .in_10(bitcomp_5_out_4), .in_11(bitcomp_6_out_3), .in_12(bitcomp_6_out_4),
    .in_13(bitcomp_7_out_3), .in_14(bitcomp_7_out_4), .in_15(bitcomp_8_out_3), .in_16(bitcomp_8_out_4),
    .out_17(A___B), .out_18(B___A));

  // Notes on the sheet:
  //   A
endmodule

module L_8x8bitAND_f97c4166 (
  input  [7:0] in_1,
  output [7:0] out_2
);
endmodule

module L_8x1bitAND_f58f873e (
  input  [7:0] in_1,
  input  in_2,
  output [7:0] out_3
);

  and and_1 (out_3[6], in_1[6], in_2);
  and and_2 (out_3[7], in_1[7], in_2);
  and and_3 (out_3[0], in_1[0], in_2);
  and and_4 (out_3[1], in_1[1], in_2);
  and and_5 (out_3[2], in_1[2], in_2);
  and and_6 (out_3[3], in_1[3], in_2);
  and and_7 (out_3[4], in_1[4], in_2);
  and and_8 (out_3[5], in_1[5], in_2);
endmodule

module RAM (
  input  in_1,
  input  in_2,
  input  in_3,
  input  in_4,
  input  in_5,
  input  in_6,
  input  in_7,
  input  in_8,
  input  in_9,
  input  in_10,
  input  in_11,
  input  in_12,
  input  in_13,
  input  in_14,
  input  in_15,
  input  in_16,
  input  in_17,
  output out_18,
  output out_19,
  output out_20,
  output out_21,
  output out_22,
  output out_23,
  output out_24,
  output out_25
);

  wire and_1_out, and_2_out, and_3_out, and_4_out, and_5_out, and_6_out, and_7_out, and_8_out, and_9_out,
       and_10_out, and_11_out, and_12_out, and_13_out, and_14_out, and_15_out, and_16_out, and_17_out,
       and_18_out, and_19_out, and_20_out, and_21_out, and_22_out, and_23_out, and_24_out,
       l_8_bit_matrix_71c719cf_2_out_19, l_8_bit_matrix_71c719cf_2_out_20, l_8_bit_matrix_71c719cf_2_out_21,
       l_8_bit_matrix_71c719cf_2_out_22, l_8_bit_matrix_71c719cf_2_out_23, l_8_bit_matrix_71c719cf_2_out_24,
       l_8_bit_matrix_71c719cf_2_out_25, l_8_bit_matrix_71c719cf_2_out_26;

  and and_1 (and_1_out, ~in_11, ~in_12, ~in_13, ~in_14, ~in_15, ~in_16, ~in_17);  // AND_Gate
  L_8_Bit_Matrix_71c719cf l_8_bit_matrix_71c719cf_1 (
    .in_9(in_9), .in_10(in_10), .in_11(and_1_out), .in_12(and_2_out), .in_13(and_3_out), .in_14(and_4_out),
    .in_1(in_8), .in_2(in_7), .in_3(in_6), .in_4(in_5), .in_5(in_4), .in_6(in_3), .in_7(in_2), .in_8(in_1),
    .out_19(out_25), .out_20(out_24), .out_21(out_23), .out_22(out_22), .out_23(out_21), .out_24(out_20),
    .out_25(out_19), .out_26(out_18), .in_15(and_5_out), .in_16(and_6_out), .in_17(and_7_out),
    .in_18(and_8_out));
  and and_2 (and_2_out, ~in_11, ~in_12, ~in_13, ~in_14, ~in_15, ~in_16, in_17);  // AND_Gate
  and and_3 (and_3_out, ~in_11, ~in_12, ~in_13, ~in_14, ~in_15, in_16, ~in_17);  // AND_Gate
  and and_4 (and_4_out, ~in_11, ~in_12, ~in_13, ~in_14, ~in_15, in_16, in_17);  // AND_Gate
  and and_5 (and_5_out, ~in_11, ~in_12, ~in_13, ~in_14, in_15, ~in_16, ~in_17);  // AND_Gate
  and and_6 (and_6_out, ~in_11, ~in_12, ~in_13, ~in_14, in_15, ~in_16, in_17);  // AND_Gate
  and and_7 (and_7_out, ~in_11, ~in_12, ~in_13, ~in_14, in_15, in_16, in_17);  // AND_Gate
  and and_8 (and_8_out, ~in_11, ~in_12, ~in_13, in_14, ~in_15, ~in_16, ~in_17);  // AND_Gate
  and and_9 (and_9_out, ~in_11, ~in_12, ~in_13, in_14, ~in_15, ~in_16, in_17);  // AND_Gate
  L_8_Bit_Matrix_71c719cf l_8_bit_matrix_71c719cf_2 (
    .in_9(in_9), .in_10(in_10), .in_11(and_9_out), .in_12(and_10_out), .in_13(and_11_out),
    .in_14(and_12_out), .in_1(in_8), .in_2(in_7), .in_3(in_6), .in_4(in_5), .in_5(in_4), .in_6(in_3),
    .in_7(in_2), .in_8(in_1), .out_19(l_8_bit_matrix_71c719cf_2_out_19),
    .out_20(l_8_bit_matrix_71c719cf_2_out_20), .out_21(l_8_bit_matrix_71c719cf_2_out_21),
    .out_22(l_8_bit_matrix_71c719cf_2_out_22), .out_23(l_8_bit_matrix_71c719cf_2_out_23),
    .out_24(l_8_bit_matrix_71c719cf_2_out_24), .out_25(l_8_bit_matrix_71c719cf_2_out_25),
    .out_26(l_8_bit_matrix_71c719cf_2_out_26), .in_15(and_13_out), .in_16(and_15_out), .in_17(and_14_out),
    .in_18(and_16_out));
  and and_10 (and_10_out, ~in_11, ~in_12, ~in_13, in_14, ~in_15, in_16, ~in_17);  // AND_Gate
  and and_11 (and_11_out, ~in_11, ~in_12, ~in_13, in_14, ~in_15, in_16, in_17);  // AND_Gate
  and and_12 (and_12_out, ~in_11, ~in_12, ~in_13, in_14, in_15, ~in_16, ~in_17);  // AND_Gate
  and and_13 (and_13_out, ~in_11, ~in_12, ~in_13, in_14, in_15, ~in_16, in_17);  // AND_Gate
  and and_14 (and_14_out, ~in_11, ~in_12, ~in_13, in_14, in_15, in_16, in_17);  // AND_Gate
  and and_15 (and_15_out, ~in_11, ~in_12, ~in_13, in_14, in_15, in_16, ~in_17);  // AND_Gate
  and and_16 (and_16_out, ~in_11, ~in_12, in_13, ~in_14, ~in_15, ~in_16, ~in_17);  // AND_Gate
  and and_17 (and_17_out, ~in_11, ~in_12, in_13, ~in_14, ~in_15, ~in_16, in_17);  // AND_Gate
  L_8_Bit_Matrix_71c719cf l_8_bit_matrix_71c719cf_3 (
    .in_9(in_9), .in_10(in_10), .in_11(and_17_out), .in_12(and_18_out), .in_13(and_19_out),
    .in_14(and_20_out), .in_1(in_8), .in_2(in_7), .in_3(in_6), .in_4(in_5), .in_5(in_4), .in_6(in_3),
    .in_7(in_2), .in_8(in_1), .out_19(l_8_bit_matrix_71c719cf_2_out_19),
    .out_20(l_8_bit_matrix_71c719cf_2_out_20), .out_21(l_8_bit_matrix_71c719cf_2_out_21),
    .out_22(l_8_bit_matrix_71c719cf_2_out_22), .out_23(l_8_bit_matrix_71c719cf_2_out_23),
    .out_24(l_8_bit_matrix_71c719cf_2_out_24), .out_25(l_8_bit_matrix_71c719cf_2_out_25),
    .out_26(l_8_bit_matrix_71c719cf_2_out_26), .in_15(and_21_out), .in_16(and_23_out), .in_17(and_22_out),
    .in_18(and_24_out));
  and and_18 (and_18_out, ~in_11, ~in_12, in_13, ~in_14, ~in_15, in_16, ~in_17);  // AND_Gate
  and and_19 (and_19_out, ~in_11, ~in_12, in_13, ~in_14, ~in_15, in_16, in_17);  // AND_Gate
  and and_20 (and_20_out, ~in_11, ~in_12, in_13, ~in_14, in_15, ~in_16, ~in_17);  // AND_Gate
  and and_21 (and_21_out, ~in_11, ~in_12, in_13, ~in_14, in_15, ~in_16, in_17);  // AND_Gate
  and and_22 (and_22_out, ~in_11, ~in_12, in_13, ~in_14, in_15, in_16, in_17);  // AND_Gate
  and and_23 (and_23_out, ~in_11, ~in_12, in_13, ~in_14, in_15, in_16, ~in_17);  // AND_Gate
  and and_24 (and_24_out, ~in_11, ~in_12, in_13, in_14, ~in_15, ~in_16, ~in_17);  // AND_Gate
endmodule

module Sieben_Segment_Controller_Dezimal (
  input  in_1,
  input  in_2,
  input  in_3,
  input  in_4,
  input  in_5,
  output out_6,
  output out_7,
  output out_8,
  output out_9,
  output out_10,
  output out_11,
  output out_12,
  output out_13
);

  wire a, and_1_out, and_2_out, and_4_out, and_5_out, and_6_out, and_7_out, and_8_out, and_9_out, and_10_out,
       and_11_out;

  and and_1 (and_1_out, ~in_1, ~in_2, ~in_3, ~in_4);  // AND_Gate
  and and_2 (and_2_out, in_1, ~in_2, ~in_3, ~in_4);  // AND_Gate
  and and_3 (a, ~in_1, in_2, ~in_3, ~in_4);  // AND_Gate
  and and_4 (and_4_out, in_1, in_2, ~in_3, ~in_4);  // AND_Gate
  and and_5 (and_5_out, ~in_1, ~in_2, in_3, ~in_4);  // AND_Gate
  and and_6 (and_6_out, in_1, ~in_2, in_3, ~in_4);  // AND_Gate
  and and_7 (and_7_out, ~in_1, in_2, in_3, ~in_4);  // AND_Gate
  and and_8 (and_8_out, in_1, in_2, in_3, ~in_4);  // AND_Gate
  and and_9 (and_9_out, ~in_1, ~in_2, ~in_3, in_4);  // AND_Gate
  and and_10 (and_10_out, in_1, ~in_2, ~in_3, in_4);  // AND_Gate
  and and_11 (and_11_out, ~a, ~and_1_out, ~and_2_out, ~and_4_out, ~and_5_out, ~and_6_out, ~and_7_out, ~and_8_out, ~and_9_out, ~and_10_out);  // AND_Gate
  or or_1 (out_9, and_1_out, and_2_out, and_4_out, and_5_out, a, and_8_out, and_9_out, and_10_out);
  or or_2 (out_8, and_6_out, and_1_out, and_4_out, a, and_7_out, and_8_out, and_9_out, and_10_out);
  or or_3 (out_7, and_1_out, and_5_out, and_6_out, and_7_out, and_9_out, and_10_out);
  or or_4 (out_6, and_6_out, and_4_out, and_5_out, a, and_7_out, and_9_out, and_10_out, and_11_out);
  or or_5 (out_10, and_7_out, a, and_9_out, and_1_out);
  or or_6 (out_11, and_1_out, and_4_out, a, and_9_out, and_7_out, and_6_out, and_10_out);
  or or_7 (out_12, and_9_out, and_8_out, and_1_out, and_2_out, and_4_out, and_10_out, and_6_out, and_7_out, and_5_out);

  assign out_13 = in_5;
endmodule

module Sieben_Segment_Controller_Hexadezimal (
  input  in_1,
  input  in_2,
  input  in_3,
  input  in_4,
  input  in_5,
  output out_6,
  output out_7,
  output out_8,
  output out_9,
  output out_10,
  output out_11,
  output out_12,
  output out_13
);

  wire and_1_out, and_2_out, and_3_out, and_4_out, and_5_out, and_6_out, and_7_out, and_8_out, and_9_out,
       and_10_out, and_11_out;

  and and_1 (and_1_out, ~in_1, ~in_2, ~in_3, ~in_4);  // AND_Gate
  and and_2 (and_2_out, in_1, ~in_2, ~in_3, ~in_4);  // AND_Gate
  and and_3 (and_3_out, ~in_1, in_2, ~in_3, ~in_4);  // AND_Gate
  and and_4 (and_4_out, in_1, in_2, ~in_3, ~in_4);  // AND_Gate
  and and_5 (and_5_out, ~in_1, ~in_2, in_3, ~in_4);  // AND_Gate
  and and_6 (and_6_out, in_1, ~in_2, in_3, ~in_4);  // AND_Gate
  and and_7 (and_7_out, ~in_1, in_2, in_3, ~in_4);  // AND_Gate
  and and_8 (and_8_out, in_1, in_2, in_3, ~in_4);  // AND_Gate
  and and_9 (and_9_out, ~in_1, ~in_2, ~in_3, in_4);  // AND_Gate
  and and_10 (and_10_out, in_1, ~in_2, ~in_3, in_4);  // AND_Gate
  and and_11 (and_11_out, ~and_3_out, ~and_1_out, ~and_2_out, ~and_4_out, ~and_5_out, ~and_6_out, ~and_7_out, ~and_8_out, ~and_9_out, ~and_10_out);  // AND_Gate
  or or_1 (out_9, and_1_out, and_2_out, and_4_out, and_5_out, and_3_out, and_8_out, and_9_out, and_10_out);
  or or_2 (out_8, and_6_out, and_1_out, and_4_out, and_3_out, and_7_out, and_8_out, and_9_out, and_10_out);
  or or_3 (out_7, and_1_out, and_5_out, and_6_out, and_7_out, and_9_out, and_10_out);
  or or_4 (out_6, and_6_out, and_4_out, and_5_out, and_3_out, and_7_out, and_9_out, and_10_out, and_11_out);
  or or_5 (out_10, and_7_out, and_3_out, and_9_out, and_1_out);
  or or_6 (out_11, and_1_out, and_4_out, and_3_out, and_9_out, and_7_out, and_6_out, and_10_out);
  or or_7 (out_12, and_9_out, and_8_out, and_1_out, and_2_out, and_4_out, and_10_out, and_6_out, and_7_out, and_5_out);

  assign out_13 = in_5;
endmodule

module L_16_Bit_Display_Glied_635da3a3 (
  input  [15:0] in_1,
  input  in_2,
  output out_3,
  output out_4,
  output out_5,
  output out_6,
  output out_7,
  output out_8,
  output out_9,
  output out_10
);
endmodule

module L_8_Bit_MUX_c01a6ef4 (
  input  [7:0] in_1,
  input  [7:0] in_2,
  input  in_3,
  output out_4,
  output [7:0] out_5
);

  wire l_bit_mux_72b0574c_2_out_4, l_bit_mux_72b0574c_3_out_4, l_bit_mux_72b0574c_4_out_4,
       l_bit_mux_72b0574c_5_out_4, l_bit_mux_72b0574c_6_out_4, l_bit_mux_72b0574c_7_out_4,
       l_bit_mux_72b0574c_8_out_4;

  L_bit_MUX_72b0574c l_bit_mux_72b0574c_1 (
    .in_1(in_1[0]), .in_2(in_2[0]), .out_5(out_5[0]), .out_4(out_4), .in_3(l_bit_mux_72b0574c_2_out_4));
  L_bit_MUX_72b0574c l_bit_mux_72b0574c_2 (
    .in_1(in_1[1]), .in_2(in_2[1]), .out_5(out_5[1]), .out_4(l_bit_mux_72b0574c_2_out_4),
    .in_3(l_bit_mux_72b0574c_3_out_4));
  L_bit_MUX_72b0574c l_bit_mux_72b0574c_3 (
    .in_1(in_1[2]), .in_2(in_2[2]), .out_5(out_5[2]), .out_4(l_bit_mux_72b0574c_3_out_4),
    .in_3(l_bit_mux_72b0574c_4_out_4));
  L_bit_MUX_72b0574c l_bit_mux_72b0574c_4 (
    .in_1(in_1[3]), .in_2(in_2[3]), .out_5(out_5[3]), .out_4(l_bit_mux_72b0574c_4_out_4),
    .in_3(l_bit_mux_72b0574c_5_out_4));
  L_bit_MUX_72b0574c l_bit_mux_72b0574c_5 (
    .in_1(in_1[4]), .in_2(in_2[4]), .out_5(out_5[4]), .out_4(l_bit_mux_72b0574c_5_out_4),
    .in_3(l_bit_mux_72b0574c_6_out_4));
  L_bit_MUX_72b0574c l_bit_mux_72b0574c_6 (
    .in_1(in_1[5]), .in_2(in_2[5]), .out_5(out_5[5]), .out_4(l_bit_mux_72b0574c_6_out_4),
    .in_3(l_bit_mux_72b0574c_7_out_4));
  L_bit_MUX_72b0574c l_bit_mux_72b0574c_7 (
    .in_1(in_1[6]), .in_2(in_2[6]), .out_5(out_5[6]), .out_4(l_bit_mux_72b0574c_7_out_4),
    .in_3(l_bit_mux_72b0574c_8_out_4));
  L_bit_MUX_72b0574c l_bit_mux_72b0574c_8 (
    .in_1(in_1[7]), .in_2(in_2[7]), .out_5(out_5[7]), .out_4(l_bit_mux_72b0574c_8_out_4), .in_3(in_3));
endmodule

module L_8_Bit_Matrix_71c719cf (
  input  in_1,
  input  in_2,
  input  in_3,
  input  in_4,
  input  in_5,
  input  in_6,
  input  in_7,
  input  in_8,
  input  in_9,
  input  in_10,
  input  in_11,
  input  in_12,
  input  in_13,
  input  in_14,
  input  in_15,
  input  in_16,
  input  in_17,
  input  in_18,
  output out_19,
  output out_20,
  output out_21,
  output out_22,
  output out_23,
  output out_24,
  output out_25,
  output out_26
);

  wire and_1_out, and_2_out, and_3_out, and_4_out, and_5_out, and_6_out, and_7_out, and_8_out, and_9_out,
       and_10_out, and_11_out, and_12_out, and_13_out, and_14_out, and_15_out, and_16_out, button_1_out,
       l_8_bit_register_070384ab_1_out_27, l_8_bit_register_070384ab_1_out_28,
       l_8_bit_register_070384ab_1_out_29, l_8_bit_register_070384ab_1_out_30,
       l_8_bit_register_070384ab_1_out_31, l_8_bit_register_070384ab_1_out_32,
       l_8_bit_register_070384ab_1_out_33, l_8_bit_register_070384ab_1_out_34,
       l_8_bit_register_070384ab_2_out_19, l_8_bit_register_070384ab_2_out_20,
       l_8_bit_register_070384ab_2_out_21, l_8_bit_register_070384ab_2_out_22,
       l_8_bit_register_070384ab_2_out_23, l_8_bit_register_070384ab_2_out_24,
       l_8_bit_register_070384ab_2_out_25, l_8_bit_register_070384ab_2_out_26,
       l_8_bit_register_070384ab_2_out_27, l_8_bit_register_070384ab_2_out_28,
       l_8_bit_register_070384ab_2_out_29, l_8_bit_register_070384ab_2_out_30,
       l_8_bit_register_070384ab_2_out_31, l_8_bit_register_070384ab_2_out_32,
       l_8_bit_register_070384ab_2_out_33, l_8_bit_register_070384ab_2_out_34,
       l_8_bit_register_070384ab_3_out_19, l_8_bit_register_070384ab_3_out_20,
       l_8_bit_register_070384ab_3_out_21, l_8_bit_register_070384ab_3_out_22,
       l_8_bit_register_070384ab_3_out_23, l_8_bit_register_070384ab_3_out_24,
       l_8_bit_register_070384ab_3_out_25, l_8_bit_register_070384ab_3_out_26,
       l_8_bit_register_070384ab_3_out_27, l_8_bit_register_070384ab_3_out_28,
       l_8_bit_register_070384ab_3_out_29, l_8_bit_register_070384ab_3_out_30,
       l_8_bit_register_070384ab_3_out_31, l_8_bit_register_070384ab_3_out_32,
       l_8_bit_register_070384ab_3_out_33, l_8_bit_register_070384ab_3_out_34,
       l_8_bit_register_070384ab_4_out_19, l_8_bit_register_070384ab_4_out_20,
       l_8_bit_register_070384ab_4_out_21, l_8_bit_register_070384ab_4_out_22,
       l_8_bit_register_070384ab_4_out_23, l_8_bit_register_070384ab_4_out_24,
       l_8_bit_register_070384ab_4_out_25, l_8_bit_register_070384ab_4_out_26,
       l_8_bit_register_070384ab_4_out_27, l_8_bit_register_070384ab_4_out_28,
       l_8_bit_register_070384ab_4_out_29, l_8_bit_register_070384ab_4_out_30,
       l_8_bit_register_070384ab_4_out_31, l_8_bit_register_070384ab_4_out_32,
       l_8_bit_register_070384ab_4_out_33, l_8_bit_register_070384ab_4_out_34,
       l_8_bit_register_070384ab_5_out_19, l_8_bit_register_070384ab_5_out_20,
       l_8_bit_register_070384ab_5_out_21, l_8_bit_register_070384ab_5_out_22,
       l_8_bit_register_070384ab_5_out_23, l_8_bit_register_070384ab_5_out_24,
       l_8_bit_register_070384ab_5_out_25, l_8_bit_register_070384ab_5_out_26,
       l_8_bit_register_070384ab_5_out_27, l_8_bit_register_070384ab_5_out_28,
       l_8_bit_register_070384ab_5_out_29, l_8_bit_register_070384ab_5_out_30,
       l_8_bit_register_070384ab_5_out_31, l_8_bit_register_070384ab_5_out_32,
       l_8_bit_register_070384ab_5_out_33, l_8_bit_register_070384ab_5_out_34,
       l_8_bit_register_070384ab_6_out_19, l_8_bit_register_070384ab_6_out_20,
       l_8_bit_register_070384ab_6_out_21, l_8_bit_register_070384ab_6_out_22,
       l_8_bit_register_070384ab_6_out_23, l_8_bit_register_070384ab_6_out_24,
       l_8_bit_register_070384ab_6_out_25, l_8_bit_register_070384ab_6_out_26,
       l_8_bit_register_070384ab_6_out_27, l_8_bit_register_070384ab_6_out_28,
       l_8_bit_register_070384ab_6_out_29, l_8_bit_register_070384ab_6_out_30,
       l_8_bit_register_070384ab_6_out_31, l_8_bit_register_070384ab_6_out_32,
       l_8_bit_register_070384ab_6_out_33, l_8_bit_register_070384ab_6_out_34,
       l_8_bit_register_070384ab_7_out_19, l_8_bit_register_070384ab_7_out_20,
       l_8_bit_register_070384ab_7_out_21, l_8_bit_register_070384ab_7_out_22,
       l_8_bit_register_070384ab_7_out_23, l_8_bit_register_070384ab_7_out_24,
       l_8_bit_register_070384ab_7_out_25, l_8_bit_register_070384ab_7_out_26,
       l_8_bit_register_070384ab_7_out_27, l_8_bit_register_070384ab_7_out_28,
       l_8_bit_register_070384ab_7_out_29, l_8_bit_register_070384ab_7_out_30,
       l_8_bit_register_070384ab_7_out_31, l_8_bit_register_070384ab_7_out_32,
       l_8_bit_register_070384ab_7_out_33, l_8_bit_register_070384ab_7_out_34,
       l_8_bit_register_070384ab_8_out_19, l_8_bit_register_070384ab_8_out_20,
       l_8_bit_register_070384ab_8_out_21, l_8_bit_register_070384ab_8_out_22,
       l_8_bit_register_070384ab_8_out_23, l_8_bit_register_070384ab_8_out_24,
       l_8_bit_register_070384ab_8_out_25, l_8_bit_register_070384ab_8_out_26;

  and and_1 (and_1_out, in_10, in_11);
  and and_2 (and_2_out, in_11, in_9);
  and and_3 (and_3_out, in_10, in_12);
  and and_4 (and_4_out, in_12, in_9);
  and and_5 (and_5_out, in_10, in_13);
  and and_6 (and_6_out, in_13, in_9);
  and and_7 (and_7_out, in_10, in_14);
  and and_8 (and_8_out, in_14, in_9);
  and and_9 (and_9_out, in_10, in_15);
  and and_10 (and_10_out, in_15, in_9);
  and and_11 (and_11_out, in_10, in_16);
  and and_12 (and_12_out, in_16, in_9);
  and and_13 (and_13_out, in_10, in_17);
  and and_14 (and_14_out, in_17, in_9);
  and and_15 (and_15_out, in_10, in_18);
  and and_16 (and_16_out, in_18, in_9);
  L_8_Bit_Register_070384ab l_8_bit_register_070384ab_1 (
    .in_9(and_1_out), .in_10(and_2_out), .in_1(in_1), .out_19(out_19), .in_2(in_2), .out_20(out_20),
    .in_3(in_3), .out_21(out_21), .in_4(in_4), .out_22(out_22), .in_5(in_5), .out_23(out_23), .in_6(in_6),
    .out_24(out_24), .in_7(in_7), .out_25(out_25), .in_8(in_8), .out_26(out_26),
    .out_27(l_8_bit_register_070384ab_1_out_27), .out_28(l_8_bit_register_070384ab_1_out_28),
    .out_29(l_8_bit_register_070384ab_1_out_29), .out_30(l_8_bit_register_070384ab_1_out_30),
    .out_31(l_8_bit_register_070384ab_1_out_31), .out_32(l_8_bit_register_070384ab_1_out_32),
    .out_33(l_8_bit_register_070384ab_1_out_33), .out_34(l_8_bit_register_070384ab_1_out_34),
    .in_11(l_8_bit_register_070384ab_2_out_19), .in_12(l_8_bit_register_070384ab_2_out_20),
    .in_13(l_8_bit_register_070384ab_2_out_21), .in_14(l_8_bit_register_070384ab_2_out_22),
    .in_15(l_8_bit_register_070384ab_2_out_23), .in_16(l_8_bit_register_070384ab_2_out_24),
    .in_17(l_8_bit_register_070384ab_2_out_25), .in_18(l_8_bit_register_070384ab_2_out_26));
  L_8_Bit_Register_070384ab l_8_bit_register_070384ab_2 (
    .in_9(and_3_out), .in_10(and_4_out), .in_1(l_8_bit_register_070384ab_1_out_27),
    .out_19(l_8_bit_register_070384ab_2_out_19), .in_2(l_8_bit_register_070384ab_1_out_28),
    .out_20(l_8_bit_register_070384ab_2_out_20), .in_3(l_8_bit_register_070384ab_1_out_29),
    .out_21(l_8_bit_register_070384ab_2_out_21), .in_4(l_8_bit_register_070384ab_1_out_30),
    .out_22(l_8_bit_register_070384ab_2_out_22), .in_5(l_8_bit_register_070384ab_1_out_31),
    .out_23(l_8_bit_register_070384ab_2_out_23), .in_6(l_8_bit_register_070384ab_1_out_32),
    .out_24(l_8_bit_register_070384ab_2_out_24), .in_7(l_8_bit_register_070384ab_1_out_33),
    .out_25(l_8_bit_register_070384ab_2_out_25), .in_8(l_8_bit_register_070384ab_1_out_34),
    .out_26(l_8_bit_register_070384ab_2_out_26), .out_27(l_8_bit_register_070384ab_2_out_27),
    .out_28(l_8_bit_register_070384ab_2_out_28), .out_29(l_8_bit_register_070384ab_2_out_29),
    .out_30(l_8_bit_register_070384ab_2_out_30), .out_31(l_8_bit_register_070384ab_2_out_31),
    .out_32(l_8_bit_register_070384ab_2_out_32), .out_33(l_8_bit_register_070384ab_2_out_33),
    .out_34(l_8_bit_register_070384ab_2_out_34), .in_11(l_8_bit_register_070384ab_3_out_19),
    .in_12(l_8_bit_register_070384ab_3_out_20), .in_13(l_8_bit_register_070384ab_3_out_21),
    .in_14(l_8_bit_register_070384ab_3_out_22), .in_15(l_8_bit_register_070384ab_3_out_23),
    .in_16(l_8_bit_register_070384ab_3_out_24), .in_17(l_8_bit_register_070384ab_3_out_25),
    .in_18(l_8_bit_register_070384ab_3_out_26));
  L_8_Bit_Register_070384ab l_8_bit_register_070384ab_3 (
    .in_9(and_5_out), .in_10(and_6_out), .in_1(l_8_bit_register_070384ab_2_out_27),
    .out_19(l_8_bit_register_070384ab_3_out_19), .in_2(l_8_bit_register_070384ab_2_out_28),
    .out_20(l_8_bit_register_070384ab_3_out_20), .in_3(l_8_bit_register_070384ab_2_out_29),
    .out_21(l_8_bit_register_070384ab_3_out_21), .in_4(l_8_bit_register_070384ab_2_out_30),
    .out_22(l_8_bit_register_070384ab_3_out_22), .in_5(l_8_bit_register_070384ab_2_out_31),
    .out_23(l_8_bit_register_070384ab_3_out_23), .in_6(l_8_bit_register_070384ab_2_out_32),
    .out_24(l_8_bit_register_070384ab_3_out_24), .in_7(l_8_bit_register_070384ab_2_out_33),
    .out_25(l_8_bit_register_070384ab_3_out_25), .in_8(l_8_bit_register_070384ab_2_out_34),
    .out_26(l_8_bit_register_070384ab_3_out_26), .out_27(l_8_bit_register_070384ab_3_out_27),
    .out_28(l_8_bit_register_070384ab_3_out_28), .out_29(l_8_bit_register_070384ab_3_out_29),
    .out_30(l_8_bit_register_070384ab_3_out_30), .out_31(l_8_bit_register_070384ab_3_out_31),
    .out_32(l_8_bit_register_070384ab_3_out_32), .out_33(l_8_bit_register_070384ab_3_out_33),
    .out_34(l_8_bit_register_070384ab_3_out_34), .in_11(l_8_bit_register_070384ab_4_out_19),
    .in_12(l_8_bit_register_070384ab_4_out_20), .in_13(l_8_bit_register_070384ab_4_out_21),
    .in_14(l_8_bit_register_070384ab_4_out_22), .in_15(l_8_bit_register_070384ab_4_out_23),
    .in_16(l_8_bit_register_070384ab_4_out_24), .in_17(l_8_bit_register_070384ab_4_out_25),
    .in_18(l_8_bit_register_070384ab_4_out_26));
  L_8_Bit_Register_070384ab l_8_bit_register_070384ab_4 (
    .in_9(and_7_out), .in_10(and_8_out), .in_1(l_8_bit_register_070384ab_3_out_27),
    .out_19(l_8_bit_register_070384ab_4_out_19), .in_2(l_8_bit_register_070384ab_3_out_28),
    .out_20(l_8_bit_register_070384ab_4_out_20), .in_3(l_8_bit_register_070384ab_3_out_29),
    .out_21(l_8_bit_register_070384ab_4_out_21), .in_4(l_8_bit_register_070384ab_3_out_30),
    .out_22(l_8_bit_register_070384ab_4_out_22), .in_5(l_8_bit_register_070384ab_3_out_31),
    .out_23(l_8_bit_register_070384ab_4_out_23), .in_6(l_8_bit_register_070384ab_3_out_32),
    .out_24(l_8_bit_register_070384ab_4_out_24), .in_7(l_8_bit_register_070384ab_3_out_33),
    .out_25(l_8_bit_register_070384ab_4_out_25), .in_8(l_8_bit_register_070384ab_3_out_34),
    .out_26(l_8_bit_register_070384ab_4_out_26), .out_27(l_8_bit_register_070384ab_4_out_27),
    .out_28(l_8_bit_register_070384ab_4_out_28), .out_29(l_8_bit_register_070384ab_4_out_29),
    .out_30(l_8_bit_register_070384ab_4_out_30), .out_31(l_8_bit_register_070384ab_4_out_31),
    .out_32(l_8_bit_register_070384ab_4_out_32), .out_33(l_8_bit_register_070384ab_4_out_33),
    .out_34(l_8_bit_register_070384ab_4_out_34), .in_11(l_8_bit_register_070384ab_5_out_19),
    .in_12(l_8_bit_register_070384ab_5_out_20), .in_13(l_8_bit_register_070384ab_5_out_21),
    .in_14(l_8_bit_register_070384ab_5_out_22), .in_15(l_8_bit_register_070384ab_5_out_23),
    .in_16(l_8_bit_register_070384ab_5_out_24), .in_17(l_8_bit_register_070384ab_5_out_25),
    .in_18(l_8_bit_register_070384ab_5_out_26));
  L_8_Bit_Register_070384ab l_8_bit_register_070384ab_5 (
    .in_9(and_9_out), .in_10(and_10_out), .in_1(l_8_bit_register_070384ab_4_out_27),
    .out_19(l_8_bit_register_070384ab_5_out_19), .in_2(l_8_bit_register_070384ab_4_out_28),
    .out_20(l_8_bit_register_070384ab_5_out_20), .in_3(l_8_bit_register_070384ab_4_out_29),
    .out_21(l_8_bit_register_070384ab_5_out_21), .in_4(l_8_bit_register_070384ab_4_out_30),
    .out_22(l_8_bit_register_070384ab_5_out_22), .in_5(l_8_bit_register_070384ab_4_out_31),
    .out_23(l_8_bit_register_070384ab_5_out_23), .in_6(l_8_bit_register_070384ab_4_out_32),
    .out_24(l_8_bit_register_070384ab_5_out_24), .in_7(l_8_bit_register_070384ab_4_out_33),
    .out_25(l_8_bit_register_070384ab_5_out_25), .in_8(l_8_bit_register_070384ab_4_out_34),
    .out_26(l_8_bit_register_070384ab_5_out_26), .out_27(l_8_bit_register_070384ab_5_out_27),
    .out_28(l_8_bit_register_070384ab_5_out_28), .out_29(l_8_bit_register_070384ab_5_out_29),
    .out_30(l_8_bit_register_070384ab_5_out_30), .out_31(l_8_bit_register_070384ab_5_out_31),
    .out_32(l_8_bit_register_070384ab_5_out_32), .out_33(l_8_bit_register_070384ab_5_out_33),
    .out_34(l_8_bit_register_070384ab_5_out_34), .in_11(l_8_bit_register_070384ab_6_out_19),
    .in_12(l_8_bit_register_070384ab_6_out_20), .in_13(l_8_bit_register_070384ab_6_out_21),
    .in_14(l_8_bit_register_070384ab_6_out_22), .in_15(l_8_bit_register_070384ab_6_out_23),
    .in_16(l_8_bit_register_070384ab_6_out_24), .in_17(l_8_bit_register_070384ab_6_out_25),
    .in_18(l_8_bit_register_070384ab_6_out_26));
  L_8_Bit_Register_070384ab l_8_bit_register_070384ab_6 (
    .in_9(and_11_out), .in_10(and_12_out), .in_1(l_8_bit_register_070384ab_5_out_27),
    .out_19(l_8_bit_register_070384ab_6_out_19), .in_2(l_8_bit_register_070384ab_5_out_28),
    .out_20(l_8_bit_register_070384ab_6_out_20), .in_3(l_8_bit_register_070384ab_5_out_29),
    .out_21(l_8_bit_register_070384ab_6_out_21), .in_4(l_8_bit_register_070384ab_5_out_30),
    .out_22(l_8_bit_register_070384ab_6_out_22), .in_5(l_8_bit_register_070384ab_5_out_31),
    .out_23(l_8_bit_register_070384ab_6_out_23), .in_6(l_8_bit_register_070384ab_5_out_32),
    .out_24(l_8_bit_register_070384ab_6_out_24), .in_7(l_8_bit_register_070384ab_5_out_33),
    .out_25(l_8_bit_register_070384ab_6_out_25), .in_8(l_8_bit_register_070384ab_5_out_34),
    .out_26(l_8_bit_register_070384ab_6_out_26), .out_27(l_8_bit_register_070384ab_6_out_27),
    .out_28(l_8_bit_register_070384ab_6_out_28), .out_29(l_8_bit_register_070384ab_6_out_29),
    .out_30(l_8_bit_register_070384ab_6_out_30), .out_31(l_8_bit_register_070384ab_6_out_31),
    .out_32(l_8_bit_register_070384ab_6_out_32), .out_33(l_8_bit_register_070384ab_6_out_33),
    .out_34(l_8_bit_register_070384ab_6_out_34), .in_11(l_8_bit_register_070384ab_7_out_19),
    .in_12(l_8_bit_register_070384ab_7_out_20), .in_13(l_8_bit_register_070384ab_7_out_21),
    .in_14(l_8_bit_register_070384ab_7_out_22), .in_15(l_8_bit_register_070384ab_7_out_23),
    .in_16(l_8_bit_register_070384ab_7_out_24), .in_17(l_8_bit_register_070384ab_7_out_25),
    .in_18(l_8_bit_register_070384ab_7_out_26));
  L_8_Bit_Register_070384ab l_8_bit_register_070384ab_7 (
    .in_9(and_13_out), .in_10(and_14_out), .in_1(l_8_bit_register_070384ab_6_out_27),
    .out_19(l_8_bit_register_070384ab_7_out_19), .in_2(l_8_bit_register_070384ab_6_out_28),
    .out_20(l_8_bit_register_070384ab_7_out_20), .in_3(l_8_bit_register_070384ab_6_out_29),
    .out_21(l_8_bit_register_070384ab_7_out_21), .in_4(l_8_bit_register_070384ab_6_out_30),
    .out_22(l_8_bit_register_070384ab_7_out_22), .in_5(l_8_bit_register_070384ab_6_out_31),
    .out_23(l_8_bit_register_070384ab_7_out_23), .in_6(l_8_bit_register_070384ab_6_out_32),
    .out_24(l_8_bit_register_070384ab_7_out_24), .in_7(l_8_bit_register_070384ab_6_out_33),
    .out_25(l_8_bit_register_070384ab_7_out_25), .in_8(l_8_bit_register_070384ab_6_out_34),
    .out_26(l_8_bit_register_070384ab_7_out_26), .out_27(l_8_bit_register_070384ab_7_out_27),
    .out_28(l_8_bit_register_070384ab_7_out_28), .out_29(l_8_bit_register_070384ab_7_out_29),
    .out_30(l_8_bit_register_070384ab_7_out_30), .out_31(l_8_bit_register_070384ab_7_out_31),
    .out_32(l_8_bit_register_070384ab_7_out_32), .out_33(l_8_bit_register_070384ab_7_out_33),
    .out_34(l_8_bit_register_070384ab_7_out_34), .in_11(l_8_bit_register_070384ab_8_out_19),
    .in_12(l_8_bit_register_070384ab_8_out_20), .in_13(l_8_bit_register_070384ab_8_out_21),
    .in_14(l_8_bit_register_070384ab_8_out_22), .in_15(l_8_bit_register_070384ab_8_out_23),
    .in_16(l_8_bit_register_070384ab_8_out_24), .in_17(l_8_bit_register_070384ab_8_out_25),
    .in_18(l_8_bit_register_070384ab_8_out_26));
  L_8_Bit_Register_070384ab l_8_bit_register_070384ab_8 (
    .in_9(and_15_out), .in_10(and_16_out), .in_1(l_8_bit_register_070384ab_7_out_27),
    .out_19(l_8_bit_register_070384ab_8_out_19), .in_2(l_8_bit_register_070384ab_7_out_28),
    .out_20(l_8_bit_register_070384ab_8_out_20), .in_3(l_8_bit_register_070384ab_7_out_29),
    .out_21(l_8_bit_register_070384ab_8_out_21), .in_4(l_8_bit_register_070384ab_7_out_30),
    .out_22(l_8_bit_register_070384ab_8_out_22), .in_5(l_8_bit_register_070384ab_7_out_31),
    .out_23(l_8_bit_register_070384ab_8_out_23), .in_6(l_8_bit_register_070384ab_7_out_32),
    .out_24(l_8_bit_register_070384ab_8_out_24), .in_7(l_8_bit_register_070384ab_7_out_33),
    .out_25(l_8_bit_register_070384ab_8_out_25), .in_8(l_8_bit_register_070384ab_7_out_34),
    .out_26(l_8_bit_register_070384ab_8_out_26), .in_11(button_1_out), .in_12(button_1_out),
    .in_13(button_1_out), .in_14(button_1_out), .in_15(button_1_out), .in_16(button_1_out),
    .in_17(button_1_out), .in_18(button_1_out));  // open: out_27, out_28, out_29, out_30, out_31, out_32, out_33, out_34
  Button button_1 (.out(button_1_out));
endmodule

module L_bit_MUX_72b0574c (
  input  in_1,
  input  in_2,
  input  in_3,
  output out_4,
  output out_5
);

  wire and_1_out, and_2_out;

  and and_1 (and_1_out, in_1, ~in_3);  // AND_Gate
  or or_1 (out_5, and_1_out, and_2_out);
  and and_2 (and_2_out, in_3, in_2);

  assign out_4 = in_3;
endmodule

module L_8_Bit_Register_070384ab (
  input  in_1,
  input  in_2,
  input  in_3,
  input  in_4,
  input  in_5,
  input  in_6,
  input  in_7,
  input  in_8,
  input  in_9,
  input  in_10,
  input  in_11,
  input  in_12,
  input  in_13,
  input  in_14,
  input  in_15,
  input  in_16,
  input  in_17,
  input  in_18,
  output out_19,
  output out_20,
  output out_21,
  output out_22,
  output out_23,
  output out_24,
  output out_25,
  output out_26,
  output out_27,
  output out_28,
  output out_29,
  output out_30,
  output out_31,
  output out_32,
  output out_33,
  output out_34
);

  wire sr_latch_aefa0f99_1_read, sr_latch_aefa0f99_2_read, sr_latch_aefa0f99_3_read,
       sr_latch_aefa0f99_4_read, sr_latch_aefa0f99_5_read, sr_latch_aefa0f99_6_read,
       sr_latch_aefa0f99_7_read, sr_latch_aefa0f99_8_read;

  SR_Latch_aefa0f99 sr_latch_aefa0f99_1 (
    .write(in_1), .write_enable(in_10), .read(sr_latch_aefa0f99_1_read), .read_enable(in_9));
  or or_1 (out_19, sr_latch_aefa0f99_1_read, in_11);
  SR_Latch_aefa0f99 sr_latch_aefa0f99_2 (
    .write(in_2), .write_enable(in_10), .read(sr_latch_aefa0f99_2_read), .read_enable(in_9));
  or or_2 (out_20, sr_latch_aefa0f99_2_read, in_12);
  SR_Latch_aefa0f99 sr_latch_aefa0f99_3 (
    .write(in_3), .write_enable(in_10), .read(sr_latch_aefa0f99_3_read), .read_enable(in_9));
  or or_3 (out_21, sr_latch_aefa0f99_3_read, in_13);
  SR_Latch_aefa0f99 sr_latch_aefa0f99_4 (
    .write(in_4), .write_enable(in_10), .read(sr_latch_aefa0f99_4_read), .read_enable(in_9));
  or or_4 (out_22, sr_latch_aefa0f99_4_read, in_14);
  SR_Latch_aefa0f99 sr_latch_aefa0f99_5 (
    .write(in_5), .write_enable(in_10), .read(sr_latch_aefa0f99_5_read), .read_enable(in_9));
  or or_5 (out_23, sr_latch_aefa0f99_5_read, in_15);
  SR_Latch_aefa0f99 sr_latch_aefa0f99_6 (
    .write(in_6), .write_enable(in_10), .read(sr_latch_aefa0f99_6_read), .read_enable(in_9));
  or or_6 (out_24, sr_latch_aefa0f99_6_read, in_16);
  SR_Latch_aefa0f99 sr_latch_aefa0f99_7 (
    .write(in_7), .write_enable(in_10), .read(sr_latch_aefa0f99_7_read), .read_enable(in_9));
  or or_7 (out_25, sr_latch_aefa0f99_7_read, in_17);
  SR_Latch_aefa0f99 sr_latch_aefa0f99_8 (
    .write(in_8), .write_enable(in_10), .read(sr_latch_aefa0f99_8_read), .read_enable(in_9));
  or or_8 (out_26, sr_latch_aefa0f99_8_read, in_18);

  assign out_27 = in_1;
  assign out_28 = in_2;
  assign out_29 = in_3;
  assign out_30 = in_4;
  assign out_31 = in_5;
  assign out_32 = in_6;
  assign out_33 = in_7;
  assign out_34 = in_8;
endmodule

module L_Bit_Matrix_adcdd69a (
  input  in_1,
  input  in_2,
  input  in_3,
  input  in_4,
  input  in_5,
  input  in_6,
  input  in_7,
  input  in_8,
  input  in_9,
  input  write_enable,
  input  wr,
  input  in_12,
  input  in_13,
  input  in_14,
  input  in_15,
  output out_16
);

  wire and_1_out, and_2_out, and_3_out, and_4_out, and_5_out, and_6_out, and_7_out, and_8_out, and_9_out,
       and_10_out, and_11_out, and_12_out, and_13_out, and_14_out, and_15_out, and_16_out, and_17_out,
       and_18_out, and_19_out, and_20_out, and_21_out, and_22_out, and_23_out, and_24_out, and_25_out,
       and_26_out, and_27_out, and_28_out, and_29_out, and_30_out, and_31_out, and_32_out, and_33_out,
       and_34_out, and_35_out, and_36_out, and_37_out, and_38_out, and_39_out, and_40_out, and_41_out,
       and_42_out, and_43_out, and_44_out, and_45_out, and_46_out, and_47_out, and_48_out, and_49_out,
       and_50_out, and_51_out, and_52_out, and_53_out, and_54_out, and_55_out, and_56_out, and_57_out,
       and_58_out, and_59_out, and_60_out, and_61_out, and_62_out, and_63_out, and_64_out, or_1_out,
       or_2_out, or_3_out, or_4_out, or_5_out, or_6_out, or_7_out, or_8_out, or_9_out, or_10_out, or_11_out,
       or_12_out, or_13_out, or_14_out, or_15_out, or_16_out, or_17_out, or_18_out, or_19_out, or_20_out,
       or_21_out, or_22_out, or_23_out, or_24_out, or_25_out, or_26_out, or_27_out, or_28_out, or_29_out,
       or_30_out, or_31_out, or_32_out, or_34_out, or_35_out, sr_latch_aefa0f99_1_read,
       sr_latch_aefa0f99_2_read, sr_latch_aefa0f99_3_read, sr_latch_aefa0f99_4_read,
       sr_latch_aefa0f99_5_read, sr_latch_aefa0f99_6_read, sr_latch_aefa0f99_7_read,
       sr_latch_aefa0f99_8_read, sr_latch_aefa0f99_9_read, sr_latch_aefa0f99_10_read,
       sr_latch_aefa0f99_11_read, sr_latch_aefa0f99_12_read, sr_latch_aefa0f99_13_read,
       sr_latch_aefa0f99_14_read, sr_latch_aefa0f99_15_read, sr_latch_aefa0f99_16_read,
       sr_latch_aefa0f99_17_read, sr_latch_aefa0f99_18_read, sr_latch_aefa0f99_19_read,
       sr_latch_aefa0f99_20_read, sr_latch_aefa0f99_21_read, sr_latch_aefa0f99_22_read,
       sr_latch_aefa0f99_23_read, sr_latch_aefa0f99_24_read, sr_latch_aefa0f99_25_read,
       sr_latch_aefa0f99_26_read, sr_latch_aefa0f99_27_read, sr_latch_aefa0f99_28_read,
       sr_latch_aefa0f99_29_read, sr_latch_aefa0f99_30_read, sr_latch_aefa0f99_31_read,
       sr_latch_aefa0f99_32_read;

  and and_1 (and_1_out, wr, in_12, in_2);
  SR_Latch_aefa0f99 sr_latch_aefa0f99_1 (
    .write(write_enable), .write_enable(and_2_out), .read(sr_latch_aefa0f99_1_read), .read_enable(and_1_out));
  and and_2 (and_2_out, in_1, in_12, in_2);
  and and_3 (and_3_out, wr, in_13, in_2);
  SR_Latch_aefa0f99 sr_latch_aefa0f99_2 (
    .write(write_enable), .write_enable(and_4_out), .read(sr_latch_aefa0f99_2_read), .read_enable(and_3_out));
  and and_4 (and_4_out, in_1, in_13, in_2);
  and and_5 (and_5_out, wr, in_14, in_2);
  SR_Latch_aefa0f99 sr_latch_aefa0f99_3 (
    .write(write_enable), .write_enable(and_6_out), .read(sr_latch_aefa0f99_3_read), .read_enable(and_5_out));
  and and_6 (and_6_out, in_1, in_14, in_2);
  and and_7 (and_7_out, wr, in_15, in_2);
  SR_Latch_aefa0f99 sr_latch_aefa0f99_4 (
    .write(write_enable), .write_enable(and_8_out), .read(sr_latch_aefa0f99_4_read), .read_enable(and_7_out));
  and and_8 (and_8_out, in_1, in_15, in_2);
  buf or_1 (or_1_out, sr_latch_aefa0f99_1_read);  // OR_Gate
  and and_9 (and_9_out, in_1, in_12, in_3);
  buf or_2 (or_2_out, sr_latch_aefa0f99_2_read);  // OR_Gate
  and and_10 (and_10_out, in_1, in_13, in_3);
  buf or_3 (or_3_out, sr_latch_aefa0f99_3_read);  // OR_Gate
  and and_11 (and_11_out, in_1, in_14, in_3);
  buf or_4 (or_4_out, sr_latch_aefa0f99_4_read);  // OR_Gate
  and and_12 (and_12_out, in_1, in_15, in_3);
  and and_13 (and_13_out, wr, in_12, in_3);
  or or_5 (or_5_out, or_1_out, sr_latch_aefa0f99_5_read);
  SR_Latch_aefa0f99 sr_latch_aefa0f99_5 (
    .write(write_enable), .write_enable(and_9_out), .read(sr_latch_aefa0f99_5_read), .read_enable(and_13_out));
  and and_14 (and_14_out, wr, in_13, in_3);
  or or_6 (or_6_out, or_2_out, sr_latch_aefa0f99_6_read);
  SR_Latch_aefa0f99 sr_latch_aefa0f99_6 (
    .write(write_enable), .write_enable(and_10_out), .read(sr_latch_aefa0f99_6_read), .read_enable(and_14_out));
  and and_15 (and_15_out, wr, in_14, in_3);
  or or_7 (or_7_out, or_3_out, sr_latch_aefa0f99_7_read);
  SR_Latch_aefa0f99 sr_latch_aefa0f99_7 (
    .write(write_enable), .write_enable(and_11_out), .read(sr_latch_aefa0f99_7_read), .read_enable(and_15_out));
  and and_16 (and_16_out, wr, in_15, in_3);
  or or_8 (or_8_out, or_4_out, sr_latch_aefa0f99_8_read);
  SR_Latch_aefa0f99 sr_latch_aefa0f99_8 (
    .write(write_enable), .write_enable(and_12_out), .read(sr_latch_aefa0f99_8_read), .read_enable(and_16_out));
  and and_17 (and_17_out, wr, in_12, in_4);
  and and_18 (and_18_out, in_1, in_12, in_4);
  and and_19 (and_19_out, wr, in_13, in_4);
  and and_20 (and_20_out, in_1, in_13, in_4);
  and and_21 (and_21_out, wr, in_14, in_4);
  and and_22 (and_22_out, in_1, in_14, in_4);
  and and_23 (and_23_out, wr, in_15, in_4);
  and and_24 (and_24_out, in_1, in_15, in_4);
  or or_9 (or_9_out, or_5_out, sr_latch_aefa0f99_9_read);
  SR_Latch_aefa0f99 sr_latch_aefa0f99_9 (
    .write(write_enable), .write_enable(and_18_out), .read(sr_latch_aefa0f99_9_read), .read_enable(and_17_out));
  or or_10 (or_10_out, or_6_out, sr_latch_aefa0f99_10_read);
  SR_Latch_aefa0f99 sr_latch_aefa0f99_10 (
    .write(write_enable), .write_enable(and_20_out), .read(sr_latch_aefa0f99_10_read),
    .read_enable(and_19_out));
  or or_11 (or_11_out, or_7_out, sr_latch_aefa0f99_11_read);
  SR_Latch_aefa0f99 sr_latch_aefa0f99_11 (
    .write(write_enable), .write_enable(and_22_out), .read(sr_latch_aefa0f99_11_read),
    .read_enable(and_21_out));
  or or_12 (or_12_out, or_8_out, sr_latch_aefa0f99_12_read);
  SR_Latch_aefa0f99 sr_latch_aefa0f99_12 (
    .write(write_enable), .write_enable(and_24_out), .read(sr_latch_aefa0f99_12_read),
    .read_enable(and_23_out));
  and and_25 (and_25_out, wr, in_12, in_5);
  SR_Latch_aefa0f99 sr_latch_aefa0f99_13 (
    .write(write_enable), .write_enable(and_26_out), .read(sr_latch_aefa0f99_13_read),
    .read_enable(and_25_out));
  and and_26 (and_26_out, in_1, in_12, in_5);
  and and_27 (and_27_out, wr, in_13, in_5);
  SR_Latch_aefa0f99 sr_latch_aefa0f99_14 (
    .write(write_enable), .write_enable(and_28_out), .read(sr_latch_aefa0f99_14_read),
    .read_enable(and_27_out));
  and and_28 (and_28_out, in_1, in_13, in_5);
  and and_29 (and_29_out, wr, in_14, in_5);
  SR_Latch_aefa0f99 sr_latch_aefa0f99_15 (
    .write(write_enable), .write_enable(and_30_out), .read(sr_latch_aefa0f99_15_read),
    .read_enable(and_29_out));
  and and_30 (and_30_out, in_1, in_14, in_5);
  and and_31 (and_31_out, wr, in_15, in_5);
  SR_Latch_aefa0f99 sr_latch_aefa0f99_16 (
    .write(write_enable), .write_enable(and_32_out), .read(sr_latch_aefa0f99_16_read),
    .read_enable(and_31_out));
  and and_32 (and_32_out, in_1, in_15, in_5);
  or or_13 (or_13_out, or_9_out, sr_latch_aefa0f99_13_read);
  or or_14 (or_14_out, or_10_out, sr_latch_aefa0f99_14_read);
  or or_15 (or_15_out, or_11_out, sr_latch_aefa0f99_15_read);
  or or_16 (or_16_out, or_12_out, sr_latch_aefa0f99_16_read);
  and and_33 (and_33_out, wr, in_12, in_6);
  SR_Latch_aefa0f99 sr_latch_aefa0f99_17 (
    .write(write_enable), .write_enable(and_34_out), .read(sr_latch_aefa0f99_17_read),
    .read_enable(and_33_out));
  and and_34 (and_34_out, in_1, in_12, in_6);
  and and_35 (and_35_out, wr, in_13, in_6);
  SR_Latch_aefa0f99 sr_latch_aefa0f99_18 (
    .write(write_enable), .write_enable(and_36_out), .read(sr_latch_aefa0f99_18_read),
    .read_enable(and_35_out));
  and and_36 (and_36_out, in_1, in_13, in_6);
  and and_37 (and_37_out, wr, in_14, in_6);
  SR_Latch_aefa0f99 sr_latch_aefa0f99_19 (
    .write(write_enable), .write_enable(and_38_out), .read(sr_latch_aefa0f99_19_read),
    .read_enable(and_37_out));
  and and_38 (and_38_out, in_1, in_14, in_6);
  and and_39 (and_39_out, wr, in_15, in_6);
  SR_Latch_aefa0f99 sr_latch_aefa0f99_20 (
    .write(write_enable), .write_enable(and_40_out), .read(sr_latch_aefa0f99_20_read),
    .read_enable(and_39_out));
  and and_40 (and_40_out, in_1, in_15, in_6);
  or or_17 (or_17_out, or_13_out, sr_latch_aefa0f99_17_read);
  and and_41 (and_41_out, in_1, in_12, in_7);
  or or_18 (or_18_out, or_14_out, sr_latch_aefa0f99_18_read);
  and and_42 (and_42_out, in_1, in_13, in_7);
  or or_19 (or_19_out, or_15_out, sr_latch_aefa0f99_19_read);
  and and_43 (and_43_out, in_1, in_14, in_7);
  or or_20 (or_20_out, or_16_out, sr_latch_aefa0f99_20_read);
  and and_44 (and_44_out, in_1, in_15, in_7);
  and and_45 (and_45_out, wr, in_12, in_7);
  or or_21 (or_21_out, or_17_out, sr_latch_aefa0f99_21_read);
  SR_Latch_aefa0f99 sr_latch_aefa0f99_21 (
    .write(write_enable), .write_enable(and_41_out), .read(sr_latch_aefa0f99_21_read),
    .read_enable(and_45_out));
  and and_46 (and_46_out, wr, in_13, in_7);
  or or_22 (or_22_out, or_18_out, sr_latch_aefa0f99_22_read);
  SR_Latch_aefa0f99 sr_latch_aefa0f99_22 (
    .write(write_enable), .write_enable(and_42_out), .read(sr_latch_aefa0f99_22_read),
    .read_enable(and_46_out));
  and and_47 (and_47_out, wr, in_14, in_7);
  or or_23 (or_23_out, or_19_out, sr_latch_aefa0f99_23_read);
  SR_Latch_aefa0f99 sr_latch_aefa0f99_23 (
    .write(write_enable), .write_enable(and_43_out), .read(sr_latch_aefa0f99_23_read),
    .read_enable(and_47_out));
  and and_48 (and_48_out, wr, in_15, in_7);
  or or_24 (or_24_out, or_20_out, sr_latch_aefa0f99_24_read);
  SR_Latch_aefa0f99 sr_latch_aefa0f99_24 (
    .write(write_enable), .write_enable(and_44_out), .read(sr_latch_aefa0f99_24_read),
    .read_enable(and_48_out));
  and and_49 (and_49_out, wr, in_12, in_8);
  and and_50 (and_50_out, in_1, in_12, in_8);
  and and_51 (and_51_out, wr, in_13, in_8);
  and and_52 (and_52_out, in_1, in_13, in_8);
  and and_53 (and_53_out, wr, in_14, in_8);
  and and_54 (and_54_out, in_1, in_14, in_8);
  and and_55 (and_55_out, wr, in_15, in_8);
  and and_56 (and_56_out, in_1, in_15, in_8);
  or or_25 (or_25_out, or_21_out, sr_latch_aefa0f99_25_read);
  SR_Latch_aefa0f99 sr_latch_aefa0f99_25 (
    .write(write_enable), .write_enable(and_50_out), .read(sr_latch_aefa0f99_25_read),
    .read_enable(and_49_out));
  or or_26 (or_26_out, or_22_out, sr_latch_aefa0f99_26_read);
  SR_Latch_aefa0f99 sr_latch_aefa0f99_26 (
    .write(write_enable), .write_enable(and_52_out), .read(sr_latch_aefa0f99_26_read),
    .read_enable(and_51_out));
  or or_27 (or_27_out, or_23_out, sr_latch_aefa0f99_27_read);
  SR_Latch_aefa0f99 sr_latch_aefa0f99_27 (
    .write(write_enable), .write_enable(and_54_out), .read(sr_latch_aefa0f99_27_read),
    .read_enable(and_53_out));
  or or_28 (or_28_out, or_24_out, sr_latch_aefa0f99_28_read);
  SR_Latch_aefa0f99 sr_latch_aefa0f99_28 (
    .write(write_enable), .write_enable(and_56_out), .read(sr_latch_aefa0f99_28_read),
    .read_enable(and_55_out));
  and and_57 (and_57_out, wr, in_12, in_9);
  SR_Latch_aefa0f99 sr_latch_aefa0f99_29 (
    .write(write_enable), .write_enable(and_58_out), .read(sr_latch_aefa0f99_29_read),
    .read_enable(and_57_out));
  and and_58 (and_58_out, in_1, in_12, in_9);
  and and_59 (and_59_out, wr, in_13, in_9);
  SR_Latch_aefa0f99 sr_latch_aefa0f99_30 (
    .write(write_enable), .write_enable(and_60_out), .read(sr_latch_aefa0f99_30_read),
    .read_enable(and_59_out));
  and and_60 (and_60_out, in_1, in_13, in_9);
  and and_61 (and_61_out, wr, in_14, in_9);
  SR_Latch_aefa0f99 sr_latch_aefa0f99_31 (
    .write(write_enable), .write_enable(and_62_out), .read(sr_latch_aefa0f99_31_read),
    .read_enable(and_61_out));
  and and_62 (and_62_out, in_1, in_14, in_9);
  and and_63 (and_63_out, wr, in_15, in_9);
  SR_Latch_aefa0f99 sr_latch_aefa0f99_32 (
    .write(write_enable), .write_enable(and_64_out), .read(sr_latch_aefa0f99_32_read),
    .read_enable(and_63_out));
  and and_64 (and_64_out, in_1, in_15, in_9);
  or or_29 (or_29_out, or_25_out, sr_latch_aefa0f99_29_read);
  or or_30 (or_30_out, or_26_out, sr_latch_aefa0f99_30_read);
  or or_31 (or_31_out, or_27_out, sr_latch_aefa0f99_31_read);
  or or_32 (or_32_out, or_28_out, sr_latch_aefa0f99_32_read);
  or or_33 (out_16, or_29_out, or_34_out);
  or or_34 (or_34_out, or_30_out, or_35_out);
  or or_35 (or_35_out, or_31_out, or_32_out);

  // Notes on the sheet:
  //   write
  //   read enable
  //   if error occurs, init
  //   all cells once (format?)
endmodule

module L_8bitoverride_e8d84573 (
  input  in_1,
  input  in_2,
  input  in_3,
  input  in_4,
  input  in_5,
  input  in_6,
  input  in_7,
  input  in_8,
  input  in_9,
  input  in_10,
  input  in_11,
  input  in_12,
  input  in_13,
  input  in_14,
  input  in_15,
  input  in_16,
  output out_17,
  output out_18
);

  wire and_1_out, and_2_out, and_3_out, and_4_out, and_5_out, and_6_out, and_7_out, and_8_out, and_9_out,
       and_10_out, and_11_out, and_12_out, and_13_out, and_14_out, not_1_out, not_2_out, not_3_out,
       not_4_out, not_5_out, not_6_out, not_7_out, not_8_out, not_9_out, not_10_out, not_11_out, not_12_out,
       not_13_out, not_14_out, or_1_out, or_2_out, or_3_out, or_4_out, or_5_out, or_6_out, or_7_out,
       or_8_out, or_9_out, or_10_out, or_11_out, or_12_out;

  not not_1 (not_1_out, in_16);
  not not_2 (not_2_out, in_15);
  or or_1 (or_1_out, in_14, in_16);
  or or_2 (or_2_out, in_15, in_13);
  and and_1 (and_1_out, in_13, not_1_out);
  and and_2 (and_2_out, in_14, not_2_out);
  not not_3 (not_3_out, or_3_out);
  or or_3 (or_3_out, in_12, or_1_out);
  not not_4 (not_4_out, or_4_out);
  or or_4 (or_4_out, in_11, or_2_out);
  and and_3 (and_3_out, in_11, not_5_out);
  and and_4 (and_4_out, in_12, not_6_out);
  not not_5 (not_5_out, or_1_out);
  not not_6 (not_6_out, or_2_out);
  or or_5 (or_5_out, in_8, or_7_out);
  or or_6 (or_6_out, in_7, or_8_out);
  not not_7 (not_7_out, or_7_out);
  or or_7 (or_7_out, in_10, or_3_out);
  or or_8 (or_8_out, in_9, or_4_out);
  not not_8 (not_8_out, or_8_out);
  and and_5 (and_5_out, in_9, not_3_out);
  and and_6 (and_6_out, in_10, not_4_out);
  or or_9 (or_9_out, in_4, or_10_out);
  or or_10 (or_10_out, in_6, or_5_out);
  not not_9 (not_9_out, or_10_out);
  or or_11 (or_11_out, in_5, or_6_out);
  not not_10 (not_10_out, or_11_out);
  and and_7 (and_7_out, in_5, not_11_out);
  and and_8 (and_8_out, in_6, not_12_out);
  not not_11 (not_11_out, or_5_out);
  not not_12 (not_12_out, or_6_out);
  and and_9 (and_9_out, in_7, not_7_out);
  and and_10 (and_10_out, in_8, not_8_out);
  and and_11 (and_11_out, in_1, not_13_out);
  not not_13 (not_13_out, or_9_out);
  not not_14 (not_14_out, or_12_out);
  or or_12 (or_12_out, in_3, or_11_out);
  and and_12 (and_12_out, in_3, not_9_out);
  and and_13 (and_13_out, in_4, not_10_out);
  and and_14 (and_14_out, in_2, not_14_out);
  or or_13 (out_17, and_11_out, and_12_out, and_7_out, and_9_out, and_5_out, and_3_out, and_1_out, in_15);
  or or_14 (out_18, and_14_out, and_13_out, and_8_out, and_10_out, and_6_out, and_4_out, and_2_out, in_16);
endmodule

module override (
  input  in_1,
  input  in_2,
  output out_3,
  output out_4
);

  wire not_1_out, not_2_out;

  not not_1 (not_1_out, in_2);
  and and_1 (out_3, in_1, not_1_out);
  and and_2 (out_4, not_2_out, in_2);
  not not_2 (not_2_out, in_1);
endmodule

module SR_Latch_aefa0f99 (
  input  write,
  input  read_enable,
  input  write_enable,
  output read
);

  wire and_1_out, and_3_out, nand_1_out, or_1_out;

  and and_1 (and_1_out, write, write_enable);
  or or_1 (or_1_out, and_3_out, and_1_out);
  nand nand_1 (nand_1_out, ~write, write_enable);  // NAND_Gate
  and and_2 (read, and_3_out, read_enable);
  and and_3 (and_3_out, or_1_out, nand_1_out);
endmodule

module HA (
  input  in_1,
  input  in_2,
  output out_3,
  output out_4
);

  xor xor_1 (out_3, in_1, in_2);
  and and_1 (out_4, in_1, in_2);
endmodule

module VA (
  input  in_1,
  input  in_2,
  input  in_3,
  output out_4,
  output out_5
);

  wire and_1_out, and_2_out, and_3_out;

  xor xor_1 (out_4, in_1, in_2, in_3);
  and and_1 (and_1_out, in_2, in_3);
  and and_2 (and_2_out, in_2, in_1);
  and and_3 (and_3_out, in_3, in_1);
  or or_1 (out_5, and_1_out, and_2_out, and_3_out);
endmodule

module miniMUL (
  input  in_1,
  input  in_2,
  input  in_3,
  input  in_4,
  input  in_5,
  input  in_6,
  input  in_7,
  input  in_8,
  output out_9,
  output out_10,
  output out_11,
  output out_12,
  output out_13,
  output out_14,
  output out_15,
  output out_16
);

  wire and_2_out, and_3_out, and_4_out, and_5_out, and_6_out, and_7_out, and_8_out, and_9_out, and_10_out,
       and_11_out, and_12_out, and_13_out, and_14_out, and_15_out, and_16_out, ha_1_out_4, ha_2_out_4,
       ha_3_out_4, ha_4_out_4, va_1_out_4, va_1_out_5, va_2_out_4, va_2_out_5, va_3_out_4, va_3_out_5,
       va_4_out_4, va_4_out_5, va_5_out_4, va_5_out_5, va_6_out_4, va_6_out_5, va_7_out_5;

  and and_1 (out_9, in_5, in_1);
  and and_2 (and_2_out, in_6, in_1);
  and and_3 (and_3_out, in_7, in_1);
  and and_4 (and_4_out, in_8, in_1);
  and and_5 (and_5_out, in_7, in_2);
  and and_6 (and_6_out, in_8, in_2);
  and and_7 (and_7_out, in_5, in_2);
  and and_8 (and_8_out, in_6, in_2);
  and and_9 (and_9_out, in_5, in_3);
  and and_10 (and_10_out, in_6, in_3);
  and and_11 (and_11_out, in_7, in_3);
  and and_12 (and_12_out, in_8, in_3);
  and and_13 (and_13_out, in_5, in_4);
  and and_14 (and_14_out, in_6, in_4);
  and and_15 (and_15_out, in_7, in_4);
  and and_16 (and_16_out, in_8, in_4);
  HA ha_1 (.in_1(and_2_out), .in_2(and_7_out), .out_3(out_10), .out_4(ha_1_out_4));
  VA va_1 (.in_1(and_3_out), .in_2(and_8_out), .in_3(ha_1_out_4), .out_4(va_1_out_4), .out_5(va_1_out_5));
  VA va_2 (.in_1(and_4_out), .in_2(and_5_out), .in_3(va_1_out_5), .out_4(va_2_out_4), .out_5(va_2_out_5));
  VA va_3 (.in_1(and_6_out), .in_2(and_11_out), .in_3(va_2_out_5), .out_4(va_3_out_4), .out_5(va_3_out_5));
  VA va_4 (.in_1(and_12_out), .in_2(and_15_out), .in_3(va_3_out_5), .out_4(va_4_out_4), .out_5(va_4_out_5));
  HA ha_2 (.in_1(va_1_out_4), .in_2(and_9_out), .out_3(out_11), .out_4(ha_2_out_4));
  VA va_5 (.in_1(va_2_out_4), .in_2(and_10_out), .in_3(ha_2_out_4), .out_4(va_5_out_4), .out_5(va_5_out_5));
  HA ha_3 (.in_1(va_5_out_4), .in_2(and_13_out), .out_3(out_12), .out_4(ha_3_out_4));
  HA ha_4 (.in_1(va_6_out_4), .in_2(ha_3_out_4), .out_3(out_13), .out_4(ha_4_out_4));
  VA va_6 (.in_1(va_3_out_4), .in_2(and_14_out), .in_3(va_5_out_5), .out_4(va_6_out_4), .out_5(va_6_out_5));
  VA va_7 (.in_1(va_4_out_4), .in_2(va_6_out_5), .in_3(ha_4_out_4), .out_4(out_14), .out_5(va_7_out_5));
  VA va_8 (.in_1(va_4_out_5), .in_2(and_16_out), .in_3(va_7_out_5), .out_4(out_15), .out_5(out_16));
endmodule

module MUL_old_1884f1bb (
  input  in_1,
  input  in_2,
  input  in_3,
  input  in_4,
  input  in_5,
  input  in_6,
  input  in_7,
  input  in_8,
  input  in_9,
  input  in_10,
  input  in_11,
  input  in_12,
  input  in_13,
  input  in_14,
  input  in_15,
  input  in_16,
  output [15:0] out_17
);

  wire _5_out_5, _10_out_5, and_2_out, and_3_out, and_4_out, and_5_out, and_6_out, and_7_out, and_8_out,
       and_9_out, and_10_out, and_11_out, and_12_out, and_13_out, and_14_out, and_15_out, and_16_out,
       and_17_out, and_18_out, and_19_out, and_20_out, and_21_out, and_22_out, and_23_out, and_24_out,
       and_25_out, and_26_out, and_27_out, and_28_out, and_29_out, and_30_out, and_31_out, and_32_out,
       and_33_out, and_34_out, and_35_out, and_36_out, and_37_out, and_38_out, and_39_out, and_40_out,
       and_41_out, and_42_out, and_43_out, and_44_out, and_45_out, and_46_out, and_47_out, and_48_out,
       and_49_out, and_50_out, and_51_out, and_52_out, and_53_out, and_54_out, and_55_out, and_56_out,
       and_57_out, and_58_out, and_59_out, and_60_out, and_61_out, and_62_out, and_63_out, and_64_out,
       ha_1_out_3, ha_1_out_4, ha_2_out_3, ha_2_out_4, ha_3_out_3, ha_3_out_4, ha_4_out_3, ha_4_out_4,
       ha_5_out_3, ha_5_out_4, ha_6_out_3, ha_6_out_4, ha_7_out_4, ha_8_out_4, va_1_out_4, va_1_out_5,
       va_2_out_4, va_2_out_5, va_3_out_4, va_3_out_5, va_4_out_4, va_4_out_5, va_5_out_4, va_5_out_5,
       va_6_out_4, va_6_out_5, va_7_out_4, va_7_out_5, va_8_out_4, va_8_out_5, va_9_out_4, va_9_out_5,
       va_10_out_4, va_10_out_5, va_11_out_4, va_11_out_5, va_12_out_4, va_12_out_5, va_13_out_4,
       va_13_out_5, va_14_out_4, va_14_out_5, va_15_out_4, va_15_out_5, va_16_out_4, va_16_out_5,
       va_17_out_4, va_17_out_5, va_18_out_4, va_18_out_5, va_19_out_4, va_19_out_5, va_20_out_4,
       va_20_out_5, va_21_out_4, va_21_out_5, va_22_out_4, va_22_out_5, va_23_out_4, va_23_out_5,
       va_24_out_4, va_24_out_5, va_25_out_4, va_25_out_5, va_26_out_4, va_26_out_5, va_27_out_4,
       va_27_out_5, va_28_out_4, va_28_out_5, va_29_out_4, va_29_out_5, va_30_out_4, va_30_out_5,
       va_31_out_4, va_31_out_5, va_32_out_4, va_32_out_5, va_33_out_4, va_33_out_5, va_34_out_4,
       va_34_out_5, va_35_out_4, va_35_out_5, va_36_out_4, va_36_out_5, va_37_out_5, va_38_out_5,
       va_39_out_5, va_40_out_5, va_41_out_5, va_42_out_5, va_43_out_5, va_44_out_5, va_45_out_5;

  and and_1 (out_17[0], in_9, in_1);
  and and_2 (and_2_out, in_10, in_1);
  and and_3 (and_3_out, in_11, in_1);
  and and_4 (and_4_out, in_12, in_1);
  and and_5 (and_5_out, in_13, in_1);
  and and_6 (and_6_out, in_14, in_1);
  and and_7 (and_7_out, in_15, in_1);
  and and_8 (and_8_out, in_16, in_1);
  and and_9 (and_9_out, in_11, in_2);
  and and_10 (and_10_out, in_12, in_2);
  and and_11 (and_11_out, in_13, in_2);
  and and_12 (and_12_out, in_14, in_2);
  and and_13 (and_13_out, in_15, in_2);
  and and_14 (and_14_out, in_16, in_2);
  and and_15 (and_15_out, in_13, in_3);
  and and_16 (and_16_out, in_14, in_3);
  and and_17 (and_17_out, in_15, in_3);
  and and_18 (and_18_out, in_16, in_3);
  and and_19 (and_19_out, in_15, in_4);
  and and_20 (and_20_out, in_16, in_4);
  and and_21 (and_21_out, in_9, in_2);
  and and_22 (and_22_out, in_10, in_2);
  and and_23 (and_23_out, in_9, in_3);
  and and_24 (and_24_out, in_10, in_3);
  and and_25 (and_25_out, in_11, in_3);
  and and_26 (and_26_out, in_12, in_3);
  and and_27 (and_27_out, in_9, in_4);
  and and_28 (and_28_out, in_10, in_4);
  and and_29 (and_29_out, in_11, in_4);
  and and_30 (and_30_out, in_12, in_4);
  and and_31 (and_31_out, in_13, in_4);
  and and_32 (and_32_out, in_14, in_4);
  and and_33 (and_33_out, in_9, in_5);
  and and_34 (and_34_out, in_10, in_5);
  and and_35 (and_35_out, in_11, in_5);
  and and_36 (and_36_out, in_12, in_5);
  and and_37 (and_37_out, in_13, in_5);
  and and_38 (and_38_out, in_14, in_5);
  and and_39 (and_39_out, in_15, in_5);
  and and_40 (and_40_out, in_16, in_5);
  and and_41 (and_41_out, in_11, in_6);
  and and_42 (and_42_out, in_12, in_6);
  and and_43 (and_43_out, in_13, in_6);
  and and_44 (and_44_out, in_14, in_6);
  and and_45 (and_45_out, in_15, in_6);
  and and_46 (and_46_out, in_16, in_6);
  and and_47 (and_47_out, in_13, in_7);
  and and_48 (and_48_out, in_14, in_7);
  and and_49 (and_49_out, in_15, in_7);
  and and_50 (and_50_out, in_16, in_7);
  and and_51 (and_51_out, in_15, in_8);
  and and_52 (and_52_out, in_16, in_8);
  and and_53 (and_53_out, in_9, in_6);
  and and_54 (and_54_out, in_10, in_6);
  and and_55 (and_55_out, in_9, in_7);
  and and_56 (and_56_out, in_10, in_7);
  and and_57 (and_57_out, in_11, in_7);
  and and_58 (and_58_out, in_12, in_7);
  and and_59 (and_59_out, in_9, in_8);
  and and_60 (and_60_out, in_10, in_8);
  and and_61 (and_61_out, in_11, in_8);
  and and_62 (and_62_out, in_12, in_8);
  and and_63 (and_63_out, in_13, in_8);
  and and_64 (and_64_out, in_14, in_8);
  HA ha_1 (.in_1(and_7_out), .in_2(and_12_out), .out_3(ha_1_out_3), .out_4(ha_1_out_4));
  VA va_1 (.in_1(ha_2_out_3), .in_2(and_16_out), .in_3(ha_1_out_4), .out_4(va_1_out_4), .out_5(va_1_out_5));
  HA ha_2 (.in_1(and_8_out), .in_2(and_13_out), .out_3(ha_2_out_3), .out_4(ha_2_out_4));
  VA va_2 (.in_1(va_3_out_4), .in_2(and_32_out), .in_3(va_1_out_5), .out_4(va_2_out_4), .out_5(va_2_out_5));
  VA va_3 (.in_1(and_14_out), .in_2(and_17_out), .in_3(ha_2_out_4), .out_4(va_3_out_4), .out_5(va_3_out_5));
  VA va_4 (.in_1(va_5_out_4), .in_2(and_38_out), .in_3(va_2_out_5), .out_4(va_4_out_4), .out_5(va_4_out_5));
  VA va_5 (.in_1(and_18_out), .in_2(and_19_out), .in_3(va_3_out_5), .out_4(va_5_out_4), .out_5(va_5_out_5));
  VA va_6 (.in_1(va_7_out_4), .in_2(and_44_out), .in_3(va_4_out_5), .out_4(va_6_out_4), .out_5(va_6_out_5));
  VA va_7 (.in_1(and_20_out), .in_2(and_39_out), .in_3(va_5_out_5), .out_4(va_7_out_4), .out_5(va_7_out_5));
  VA va_8 (.in_1(va_9_out_4), .in_2(and_48_out), .in_3(va_6_out_5), .out_4(va_8_out_4), .out_5(va_8_out_5));
  VA va_9 (.in_1(and_40_out), .in_2(and_45_out), .in_3(va_7_out_5), .out_4(va_9_out_4), .out_5(va_9_out_5));
  VA va_10 (.in_1(va_11_out_4), .in_2(and_64_out), .in_3(va_8_out_5), .out_4(va_10_out_4), .out_5(va_10_out_5));
  VA va_11 (.in_1(and_46_out), .in_2(and_49_out), .in_3(va_9_out_5), .out_4(va_11_out_4), .out_5(va_11_out_5));
  VA va_12 (.in_1(and_50_out), .in_2(and_51_out), .in_3(va_11_out_5), .out_4(va_12_out_4), .out_5(va_12_out_5));
  HA ha_3 (.in_1(and_6_out), .in_2(and_11_out), .out_3(ha_3_out_3), .out_4(ha_3_out_4));
  VA va_13 (.in_1(ha_1_out_3), .in_2(and_15_out), .in_3(ha_3_out_4), .out_4(va_13_out_4), .out_5(va_13_out_5));
  VA va_14 (.in_1(va_1_out_4), .in_2(and_31_out), .in_3(va_13_out_5), .out_4(va_14_out_4), .out_5(va_14_out_5));
  VA va_15 (.in_1(va_2_out_4), .in_2(and_37_out), .in_3(va_14_out_5), .out_4(va_15_out_4), .out_5(va_15_out_5));
  VA va_16 (.in_1(va_4_out_4), .in_2(and_43_out), .in_3(va_15_out_5), .out_4(va_16_out_4), .out_5(va_16_out_5));
  VA va_17 (.in_1(va_6_out_4), .in_2(and_47_out), .in_3(va_16_out_5), .out_4(va_17_out_4), .out_5(va_17_out_5));
  VA va_18 (.in_1(va_8_out_4), .in_2(and_63_out), .in_3(va_17_out_5), .out_4(va_18_out_4), .out_5(va_18_out_5));
  HA ha_4 (.in_1(and_4_out), .in_2(and_9_out), .out_3(ha_4_out_3), .out_4(ha_4_out_4));
  HA ha_5 (.in_1(and_5_out), .in_2(and_10_out), .out_3(ha_5_out_3), .out_4(ha_5_out_4));
  VA va_19 (.in_1(ha_5_out_3), .in_2(and_25_out), .in_3(ha_4_out_4), .out_4(va_19_out_4), .out_5(va_19_out_5));
  VA va_20 (.in_1(ha_3_out_3), .in_2(and_26_out), .in_3(ha_5_out_4), .out_4(va_20_out_4), .out_5(va_20_out_5));
  VA va_21 (.in_1(va_20_out_4), .in_2(and_34_out), .in_3(va_19_out_5), .out_4(va_21_out_4), .out_5(va_21_out_5));
  VA va_22 (.in_1(va_23_out_4), .in_2(and_30_out), .in_3(va_21_out_5), .out_4(va_22_out_4), .out_5(va_22_out_5));
  VA va_23 (.in_1(va_13_out_4), .in_2(and_35_out), .in_3(va_20_out_5), .out_4(va_23_out_4), .out_5(va_23_out_5));
  VA va_24 (.in_1(va_14_out_4), .in_2(and_36_out), .in_3(va_23_out_5), .out_4(va_24_out_4), .out_5(va_24_out_5));
  VA va_25 (.in_1(va_24_out_4), .in_2(and_41_out), .in_3(va_22_out_5), .out_4(va_25_out_4), .out_5(va_25_out_5));
  VA va_26 (.in_1(va_15_out_4), .in_2(and_42_out), .in_3(va_24_out_5), .out_4(va_26_out_4), .out_5(va_26_out_5));
  VA va_27 (.in_1(va_26_out_4), .in_2(and_57_out), .in_3(va_25_out_5), .out_4(va_27_out_4), .out_5(va_27_out_5));
  VA va_28 (.in_1(va_16_out_4), .in_2(and_58_out), .in_3(va_26_out_5), .out_4(va_28_out_4), .out_5(va_28_out_5));
  VA va_29 (.in_1(va_28_out_4), .in_2(and_61_out), .in_3(va_27_out_5), .out_4(va_29_out_4), .out_5(va_29_out_5));
  VA va_30 (.in_1(va_17_out_4), .in_2(and_62_out), .in_3(va_28_out_5), .out_4(va_30_out_4), .out_5(va_30_out_5));
  HA ha_6 (.in_1(and_3_out), .in_2(and_22_out), .out_3(ha_6_out_3), .out_4(ha_6_out_4));
  VA va_31 (.in_1(ha_4_out_3), .in_2(and_24_out), .in_3(ha_6_out_4), .out_4(va_31_out_4), .out_5(va_31_out_5));
  VA va_32 (.in_1(va_19_out_4), .in_2(and_28_out), .in_3(va_31_out_5), .out_4(va_32_out_4), .out_5(va_32_out_5));
  VA va_33 (.in_1(va_21_out_4), .in_2(and_53_out), .in_3(va_32_out_5), .out_4(va_33_out_4), .out_5(va_33_out_5));
  VA va_34 (.in_1(va_22_out_4), .in_2(and_54_out), .in_3(va_33_out_5), .out_4(va_34_out_4), .out_5(va_34_out_5));
  VA va_35 (.in_1(va_25_out_4), .in_2(and_56_out), .in_3(va_34_out_5), .out_4(va_35_out_4), .out_5(va_35_out_5));
  VA va_36 (.in_1(va_27_out_4), .in_2(and_60_out), .in_3(va_35_out_5), .out_4(va_36_out_4), .out_5(va_36_out_5));
  HA ha_7 (.in_1(and_2_out), .in_2(and_21_out), .out_3(out_17[1]), .out_4(ha_7_out_4));
  VA va_37 (.in_1(ha_6_out_3), .in_2(and_23_out), .in_3(ha_7_out_4), .out_4(out_17[2]), .out_5(va_37_out_5));
  VA va_38 (.in_1(va_31_out_4), .in_2(and_27_out), .in_3(va_37_out_5), .out_4(out_17[3]), .out_5(va_38_out_5));
  VA _5 (.in_1(va_32_out_4), .in_2(and_33_out), .in_3(va_38_out_5), .out_4(out_17[4]), .out_5(_5_out_5));
  VA va_39 (.in_1(va_33_out_4), .in_2(and_29_out), .in_3(_5_out_5), .out_4(out_17[5]), .out_5(va_39_out_5));
  VA va_40 (.in_1(va_34_out_4), .in_2(and_55_out), .in_3(va_39_out_5), .out_4(out_17[6]), .out_5(va_40_out_5));
  VA va_41 (.in_1(va_35_out_4), .in_2(and_59_out), .in_3(va_40_out_5), .out_4(out_17[7]), .out_5(va_41_out_5));
  HA ha_8 (.in_1(va_36_out_4), .in_2(va_41_out_5), .out_3(out_17[8]), .out_4(ha_8_out_4));
  VA _10 (.in_1(va_29_out_4), .in_2(va_36_out_5), .in_3(ha_8_out_4), .out_4(out_17[9]), .out_5(_10_out_5));
  VA va_42 (.in_1(va_30_out_4), .in_2(va_29_out_5), .in_3(_10_out_5), .out_4(out_17[10]), .out_5(va_42_out_5));
  VA va_43 (.in_1(va_18_out_4), .in_2(va_30_out_5), .in_3(va_42_out_5), .out_4(out_17[11]), .out_5(va_43_out_5));
  VA va_44 (.in_1(va_10_out_4), .in_2(va_18_out_5), .in_3(va_43_out_5), .out_4(out_17[12]), .out_5(va_44_out_5));
  VA va_45 (.in_1(va_12_out_4), .in_2(va_10_out_5), .in_3(va_44_out_5), .out_4(out_17[13]), .out_5(va_45_out_5));
  VA _15 (.in_1(and_52_out), .in_2(va_12_out_5), .in_3(va_45_out_5), .out_4(out_17[14]), .out_5(out_17[15]));
endmodule

module BITCOMP (
  input  in_1,
  input  in_2,
  output out_3,
  output out_4
);

  wire xor_1_out;

  xor xor_1 (xor_1_out, in_1, in_2);
  and and_1 (out_3, in_1, xor_1_out);
  and and_2 (out_4, xor_1_out, in_2);
endmodule
