// Logisim project speicher.circ as structural Verilog
module SR_Zelle_Enable (
  input  write,
  input  read_enable,
  input  write_enable,
  output read
);

  wire and_1_out, and_2_out, nand_1_out, or_1_out;

  and and_1 (and_1_out, write, write_enable);
  nand nand_1 (nand_1_out, ~write, write_enable);  // NAND_Gate
  or or_1 (or_1_out, and_2_out, and_1_out);
  and and_2 (and_2_out, or_1_out, nand_1_out);
  and and_3 (read, and_2_out, read_enable);
endmodule

module SR_Zelle_Clock (
  input  clock,
  input  write,
  input  Q,
  input  set,
  input  reset,
  input  systemreset,
  output nQ,
  output out_8
);

  wire and_1_out, s_r_ff_1_q, s_r_ff_1_qn;

  and and_1 (and_1_out, write, clock);
  S_R_Flip_Flop s_r_ff_1 (
    .S(set), .clk(and_1_out), .R(reset), .Q(s_r_ff_1_q), .Qn(s_r_ff_1_qn), .reset(systemreset));  // open: preset, en
  and and_2 (nQ, Q, s_r_ff_1_q);
  and and_3 (out_8, s_r_ff_1_qn, Q);

  // Notes on the sheet:
  //   enable
  //   read enable
endmodule

module SR_Latch (
);

  wire button_1_out, button_2_out, nand_1_out, nand_2_out;

  Button button_1 (.out(button_1_out));
  Button button_2 (.out(button_2_out));
  nand nand_1 (nand_1_out, ~button_1_out, nand_2_out);  // NAND_Gate
  nand nand_2 (nand_2_out, nand_1_out, ~button_2_out);  // NAND_Gate
  LED led_1 (.in(nand_1_out));
  LED led_2 (.in(nand_2_out));
endmodule
